// Logisim project add_half_all.circ as structural Verilog: 12 circuits, main circuit main_four_add
module main_four_add (
  input  A3,
  input  A2,
  input  A1,
  input  A0,
  input  B3,
  input  B2,
  input  B1,
  input  B0,
  output Y3,
  output Y2,
  output Y1,
  output Y0,
  output CO
);

  wire one_all_add_1_co, one_all_add_2_co, one_all_add_3_co;

  one_all_add one_all_add_1 (.A(A0), .B(B0), .S(Y0), .CO(one_all_add_1_co));  // open: CI
  one_all_add one_all_add_2 (.CI(one_all_add_1_co), .A(A1), .B(B1), .S(Y1), .CO(one_all_add_2_co));
  one_all_add one_all_add_3 (.CI(one_all_add_2_co), .A(A2), .B(B2), .S(Y2), .CO(one_all_add_3_co));
  one_all_add one_all_add_4 (.CI(one_all_add_3_co), .A(A3), .B(B3), .S(Y3), .CO(CO));

  // Notes on the sheet:
  //   4位加法器
  //   2个四位数求和
endmodule

module one_half_add (
  input  A,
  input  B,
  output S,
  output C
);

  wire and_1_out, and_2_out, not_1_out, not_2_out;

  not not_1 (not_1_out, A);
  not not_2 (not_2_out, B);
  and and_1 (and_1_out, not_1_out, B);
  or or_1 (S, and_1_out, and_2_out);
  and and_2 (and_2_out, not_2_out, A);
  and and_3 (C, A, B);

  // Notes on the sheet:
  //   1位加法器（半加器）
endmodule

module two_half_add_to_one_all_add (
  input  A1,
  input  B1,
  input  C0,
  output C1,
  output S0
);

  wire one_half_add_1_c, one_half_add_1_s, one_half_add_2_c;

  one_half_add one_half_add_1 (.A(A1), .B(B1), .S(one_half_add_1_s), .C(one_half_add_1_c));
  one_half_add one_half_add_2 (.A(one_half_add_1_s), .B(C0), .S(S0), .C(one_half_add_2_c));
  or or_1 (C1, one_half_add_1_c, one_half_add_2_c);

  // Notes on the sheet:
  //   2半加器—1全加器
endmodule

module one_all_add (
  input  CI,
  input  A,
  input  B,
  output S,
  output CO
);

  wire and_1_out, and_2_out, and_3_out, and_4_out, and_5_out, and_6_out, and_7_out, not_1_out, not_2_out,
       not_3_out;

  not not_1 (not_1_out, CI);
  not not_2 (not_2_out, A);
  not not_3 (not_3_out, B);
  and and_1 (and_1_out, not_1_out, not_2_out, B);
  and and_2 (and_2_out, not_1_out, A, not_3_out);
  and and_3 (and_3_out, CI, not_2_out, not_3_out);
  and and_4 (and_4_out, CI, A, B);
  and and_5 (and_5_out, CI, A);
  and and_6 (and_6_out, CI, B);
  and and_7 (and_7_out, A, B);
  or or_1 (S, and_1_out, and_2_out, and_3_out, and_4_out);
  or or_2 (CO, and_5_out, and_6_out, and_7_out);

  // Notes on the sheet:
  //   1位全加器
endmodule

module four_minus (
  input  in_1,
  input  in_2,
  input  A3,
  input  A2,
  input  A1,
  input  A0,
  input  B3,
  input  B2,
  input  B1,
  input  B0
);

  wire four_eight_decoder_16_to_light_1_ya, four_eight_decoder_16_to_light_1_yb,
       four_eight_decoder_16_to_light_1_yc, four_eight_decoder_16_to_light_1_yd,
       four_eight_decoder_16_to_light_1_ye, four_eight_decoder_16_to_light_1_yf,
       four_eight_decoder_16_to_light_1_yg, not_1_out, not_2_out, not_3_out, not_4_out, not_5_out,
       one_all_add_1_co, one_all_add_1_s, one_all_add_2_co, one_all_add_2_s, one_all_add_3_co,
       one_all_add_3_s, one_all_add_4_co, one_all_add_4_s;

  one_all_add one_all_add_1 (.CI(in_2), .A(A0), .B(not_5_out), .S(one_all_add_1_s), .CO(one_all_add_1_co));
  one_all_add one_all_add_2 (.CI(one_all_add_1_co), .A(A1), .B(not_4_out), .S(one_all_add_2_s), .CO(one_all_add_2_co));
  one_all_add one_all_add_3 (.CI(one_all_add_2_co), .A(A2), .B(not_3_out), .S(one_all_add_3_s), .CO(one_all_add_3_co));
  not not_1 (not_1_out, one_all_add_4_co);
  LED led_1 (.in(not_1_out));
  one_all_add one_all_add_4 (.CI(one_all_add_3_co), .A(A3), .B(not_2_out), .S(one_all_add_4_s), .CO(one_all_add_4_co));
  not not_2 (not_2_out, B3);
  not not_3 (not_3_out, B2);
  not not_4 (not_4_out, B1);
  not not_5 (not_5_out, B0);
  four_eight_decoder_16_to_light four_eight_decoder_16_to_light_1 (
    .A3(one_all_add_4_s), .A2(one_all_add_3_s), .A1(one_all_add_2_s), .A0(one_all_add_1_s), .S(in_1),
    .Ye(four_eight_decoder_16_to_light_1_ye), .Yc(four_eight_decoder_16_to_light_1_yc),
    .Ya(four_eight_decoder_16_to_light_1_ya), .Yg(four_eight_decoder_16_to_light_1_yg),
    .Yf(four_eight_decoder_16_to_light_1_yf), .Yd(four_eight_decoder_16_to_light_1_yd),
    .Yb(four_eight_decoder_16_to_light_1_yb));
  _7_Segment_Display u_7_segment_display_1 (
    .g(four_eight_decoder_16_to_light_1_yg), .f(four_eight_decoder_16_to_light_1_yf),
    .a(four_eight_decoder_16_to_light_1_ya), .b(four_eight_decoder_16_to_light_1_yb),
    .e(four_eight_decoder_16_to_light_1_ye), .d(four_eight_decoder_16_to_light_1_yd),
    .c(four_eight_decoder_16_to_light_1_yc), .dp(1'b0));

  // Notes on the sheet:
  //   4位减法器
  //   2个四位数相减，LED亮说明A<B
endmodule

module four_fan_ma_add (
  input  [3:0] in_1,
  input  [3:0] in_2,
  output [3:0] out_3
);

  wire [3:0] fan_to_yuan_ma_1_a_bar, fan_to_yuan_ma_2_a_bar, three_add_1_y;

  fan_to_yuan_ma fan_to_yuan_ma_1 (.A(in_1), .A_bar(fan_to_yuan_ma_1_a_bar));
  fan_to_yuan_ma fan_to_yuan_ma_2 (.A(in_2), .A_bar(fan_to_yuan_ma_2_a_bar));
  three_add three_add_1 (.A(fan_to_yuan_ma_1_a_bar), .B(fan_to_yuan_ma_2_a_bar), .Y(three_add_1_y));
  fan_to_yuan_ma fan_to_yuan_ma_3 (.A(three_add_1_y), .A_bar(out_3));

  // Notes on the sheet:
  //   4位反码加法器
endmodule

module four_yuan_ma_add (
  input  A3,
  input  B3,
  input  A2,
  input  B2,
  input  A1,
  input  B1,
  input  A0,
  input  B0,
  input  in_9,
  input  in_10,
  input  in_11,
  input  in_12
);

  wire and_1_out, and_2_out, and_3_out, and_4_out, four_eight_decoder_16_to_light_1_ya,
       four_eight_decoder_16_to_light_1_yb, four_eight_decoder_16_to_light_1_yc,
       four_eight_decoder_16_to_light_1_yd, four_eight_decoder_16_to_light_1_ye,
       four_eight_decoder_16_to_light_1_yf, four_eight_decoder_16_to_light_1_yg,
       four_eight_decoder_16_to_light_2_ya, four_eight_decoder_16_to_light_2_yb,
       four_eight_decoder_16_to_light_2_yc, four_eight_decoder_16_to_light_2_yd,
       four_eight_decoder_16_to_light_2_ye, four_eight_decoder_16_to_light_2_yf,
       four_eight_decoder_16_to_light_2_yg, not_2_out, not_3_out, not_4_out, not_5_out, not_6_out, not_7_out,
       one_all_add_1_co, one_all_add_1_s, one_all_add_2_co, one_all_add_2_s, one_all_add_3_co,
       one_all_add_3_s, one_all_add_4_co, one_all_add_4_s, one_all_add_5_co, one_all_add_5_s,
       one_all_add_6_co, one_all_add_6_s, one_all_add_7_co, one_all_add_7_s, one_all_add_8_s, S, xnor_1_out;

  not not_1 (S, xnor_1_out);
  xnor xnor_1 (xnor_1_out, A3, B3);
  and and_1 (and_1_out, xnor_1_out, one_all_add_1_s);
  one_all_add one_all_add_1 (.CI(in_9), .A(A0), .B(B0), .S(one_all_add_1_s), .CO(one_all_add_1_co));
  one_all_add one_all_add_2 (.CI(in_10), .A(A0), .B(not_6_out), .S(one_all_add_2_s), .CO(one_all_add_2_co));
  and and_2 (and_2_out, xnor_1_out, one_all_add_3_s);
  one_all_add one_all_add_3 (.CI(one_all_add_1_co), .A(A1), .B(B1), .S(one_all_add_3_s), .CO(one_all_add_3_co));
  one_all_add one_all_add_4 (.CI(one_all_add_2_co), .A(A1), .B(not_5_out), .S(one_all_add_4_s), .CO(one_all_add_4_co));
  one_all_add one_all_add_5 (.CI(one_all_add_4_co), .A(A2), .B(not_4_out), .S(one_all_add_5_s), .CO(one_all_add_5_co));
  and and_3 (and_3_out, xnor_1_out, one_all_add_6_s);
  one_all_add one_all_add_6 (.CI(one_all_add_3_co), .A(A2), .B(B2), .S(one_all_add_6_s), .CO(one_all_add_6_co));
  one_all_add one_all_add_7 (
    .CI(one_all_add_5_co), .A(in_11), .B(not_3_out), .S(one_all_add_7_s), .CO(one_all_add_7_co));
  and and_4 (and_4_out, xnor_1_out, one_all_add_8_s);
  one_all_add one_all_add_8 (.CI(one_all_add_6_co), .A(1'b0), .B(1'b0), .S(one_all_add_8_s));  // open: CO
  not not_2 (not_2_out, one_all_add_7_co);
  LED led_1 (.in(not_2_out));
  not not_3 (not_3_out, in_12);
  not not_4 (not_4_out, B2);
  not not_5 (not_5_out, B1);
  not not_6 (not_6_out, B0);
  not not_7 (not_7_out, S);
  four_eight_decoder_16_to_light four_eight_decoder_16_to_light_1 (
    .A3(and_4_out), .A2(and_3_out), .A1(and_2_out), .A0(and_1_out), .S(not_7_out),
    .Ye(four_eight_decoder_16_to_light_1_ye), .Yc(four_eight_decoder_16_to_light_1_yc),
    .Ya(four_eight_decoder_16_to_light_1_ya), .Yg(four_eight_decoder_16_to_light_1_yg),
    .Yf(four_eight_decoder_16_to_light_1_yf), .Yd(four_eight_decoder_16_to_light_1_yd),
    .Yb(four_eight_decoder_16_to_light_1_yb));
  four_eight_decoder_16_to_light four_eight_decoder_16_to_light_2 (
    .A3(one_all_add_7_s), .A2(one_all_add_5_s), .A1(one_all_add_4_s), .A0(one_all_add_2_s), .S(S),
    .Ye(four_eight_decoder_16_to_light_2_ye), .Yc(four_eight_decoder_16_to_light_2_yc),
    .Ya(four_eight_decoder_16_to_light_2_ya), .Yg(four_eight_decoder_16_to_light_2_yg),
    .Yf(four_eight_decoder_16_to_light_2_yf), .Yd(four_eight_decoder_16_to_light_2_yd),
    .Yb(four_eight_decoder_16_to_light_2_yb));
  _7_Segment_Display u_7_segment_display_1 (
    .g(four_eight_decoder_16_to_light_1_yg), .f(four_eight_decoder_16_to_light_1_yf),
    .a(four_eight_decoder_16_to_light_1_ya), .b(four_eight_decoder_16_to_light_1_yb),
    .e(four_eight_decoder_16_to_light_1_ye), .d(four_eight_decoder_16_to_light_1_yd),
    .c(four_eight_decoder_16_to_light_1_yc), .dp(1'b0));
  _7_Segment_Display u_7_segment_display_2 (.g(S));  // open: f, a, b, e, d, c, dp
  _7_Segment_Display u_7_segment_display_3 (
    .g(four_eight_decoder_16_to_light_2_yg), .f(four_eight_decoder_16_to_light_2_yf),
    .a(four_eight_decoder_16_to_light_2_ya), .b(four_eight_decoder_16_to_light_2_yb),
    .e(four_eight_decoder_16_to_light_2_ye), .d(four_eight_decoder_16_to_light_2_yd),
    .c(four_eight_decoder_16_to_light_2_yc), .dp(1'b0));

  // Notes on the sheet:
  //   4位原码加法器
  //   4位减法器
  //   2个四位数相减，LED亮说明A<B
endmodule

module fan_to_yuan_ma (
  input  [3:0] A,
  output [3:0] A_bar
);

  xor xor_1 (A_bar[2], A[3], A[2]);
  xor xor_2 (A_bar[1], A[3], A[1]);
  xor xor_3 (A_bar[0], A[3], A[0]);

  assign A_bar[3] = A[3];

  // Notes on the sheet:
  //   原码反码转换
endmodule

module three_add (
  input  [3:0] A,
  input  [3:0] B,
  output [3:0] Y
);

  wire not_1_out, not_3_out, not_4_out, not_5_out, not_6_out, not_7_out, not_8_out, not_9_out, not_10_out,
       not_11_out, not_12_out, one_all_add_1_co, one_all_add_2_co, one_all_add_4_co, one_all_add_5_co,
       one_all_add_6_co, one_all_add_7_co, one_all_add_8_co, transmission_1_p2, transmission_2_p4,
       transmission_4_p3, xnor_1_out, xor_1_out;
  wire [2:0] one_all_add_1_s, one_all_add_4_s, one_all_add_7_s;

  xnor xnor_1 (xnor_1_out, B[3], A[3]);
  not not_1 (not_1_out, xnor_1_out);
  one_all_add one_all_add_1 (.CI(1'b0), .A(A[0]), .B(B[0]), .S(one_all_add_1_s[0]), .CO(one_all_add_1_co));
  one_all_add one_all_add_2 (.CI(one_all_add_1_co), .A(A[1]), .B(B[1]), .S(one_all_add_1_s[1]), .CO(one_all_add_2_co));
  one_all_add one_all_add_3 (.CI(one_all_add_2_co), .A(A[2]), .B(B[2]), .S(one_all_add_1_s[2]));  // open: CO
  // Transmission_Gate #(.width(4)) transmission_1: pin names not known; wires that end beside it: not_1_out, transmission_1_p2, Y
  not not_2 (transmission_1_p2, not_1_out);
  not not_3 (not_3_out, B[2]);
  not not_4 (not_4_out, B[1]);
  not not_5 (not_5_out, B[0]);
  not not_6 (not_6_out, A[2]);
  not not_7 (not_7_out, A[1]);
  not not_8 (not_8_out, A[0]);
  xor xor_1 (xor_1_out, B[3], A[3]);
  one_all_add one_all_add_4 (.CI(1'b1), .A(A[0]), .B(not_5_out), .S(one_all_add_4_s[0]), .CO(one_all_add_4_co));
  one_all_add one_all_add_5 (
    .CI(one_all_add_4_co), .A(A[1]), .B(not_4_out), .S(one_all_add_4_s[1]), .CO(one_all_add_5_co));
  one_all_add one_all_add_6 (
    .CI(one_all_add_5_co), .A(A[2]), .B(not_3_out), .S(one_all_add_4_s[2]), .CO(one_all_add_6_co));
  not not_9 (not_9_out, one_all_add_6_co);
  not not_10 (not_10_out, not_9_out);
  one_all_add one_all_add_7 (.CI(1'b1), .A(B[0]), .B(not_8_out), .S(one_all_add_7_s[0]), .CO(one_all_add_7_co));
  one_all_add one_all_add_8 (
    .CI(one_all_add_7_co), .A(B[1]), .B(not_7_out), .S(one_all_add_7_s[1]), .CO(one_all_add_8_co));
  one_all_add one_all_add_9 (.CI(one_all_add_8_co), .A(B[2]), .B(not_6_out), .S(one_all_add_7_s[2]));  // open: CO
  not not_11 (not_11_out, not_9_out);
  not not_12 (not_12_out, not_10_out);
  // Transmission_Gate #(.width(4)) transmission_2: pin names not known; wires that end beside it: {A[3], one_all_add_4_s}, not_9_out, not_11_out, transmission_2_p4
  // Transmission_Gate #(.width(4)) transmission_3: pin names not known; wires that end beside it: {B[3], one_all_add_7_s}, not_10_out, not_12_out, transmission_2_p4
  // Transmission_Gate #(.width(4)) transmission_4: pin names not known; wires that end beside it: transmission_2_p4, xor_1_out, transmission_4_p3, Y
  not not_13 (transmission_4_p3, xor_1_out);

  // Notes on the sheet:
  //   同号相加
  //   三位加法器，最高位为符号位
  //   异号相减
endmodule

module four_add_yi_chu_jian_ce (
  input  [3:0] A,
  input  [3:0] B,
  output [3:0] Y,
  output c
);

  wire one_all_add_1_co, one_all_add_2_co, one_all_add_3_co, xor_1_out;

  one_all_add one_all_add_1 (.CI(1'b0), .A(A[0]), .B(B[0]), .S(Y[0]), .CO(one_all_add_1_co));
  one_all_add one_all_add_2 (.CI(one_all_add_1_co), .A(A[1]), .B(B[1]), .S(Y[1]), .CO(one_all_add_2_co));
  one_all_add one_all_add_3 (.CI(one_all_add_2_co), .A(A[2]), .B(B[2]), .S(Y[2]), .CO(one_all_add_3_co));
  one_all_add one_all_add_4 (.CI(one_all_add_3_co), .A(A[3]), .B(B[3]), .S(Y[3]), .CO(c));
  xor xor_1 (xor_1_out, one_all_add_3_co, c);
  LED led_1 (.in(xor_1_out));

  // Notes on the sheet:
  //   4位加法器
  //   溢出检测
endmodule

module four_fan_ma_add_ez (
  input  [3:0] A,
  input  [3:0] B,
  output [3:0] Y
);

  wire [0:0] four_add_yi_chu_jian_ce_1_c;
  wire [3:0] four_add_yi_chu_jian_ce_1_y;

  four_add_yi_chu_jian_ce four_add_yi_chu_jian_ce_1 (
    .A(A), .B(B), .Y(four_add_yi_chu_jian_ce_1_y), .c(four_add_yi_chu_jian_ce_1_c[0]));
  four_add_yi_chu_jian_ce four_add_yi_chu_jian_ce_2 (
    .A(four_add_yi_chu_jian_ce_1_y), .B({3'b000, four_add_yi_chu_jian_ce_1_c[0]}), .Y(Y));  // open: c

  // Notes on the sheet:
  //   4位反码加法器（简易）
endmodule

module eight_add (
  input  B7,
  input  B6,
  input  B5,
  input  B4,
  input  B3,
  input  B2,
  input  B1,
  input  B0,
  input  A7,
  input  A6,
  input  A5,
  input  A4,
  input  A3,
  input  A2,
  input  A1,
  input  A0,
  output Y7,
  output Y6,
  output Y5,
  output Y4,
  output Y3,
  output Y2,
  output Y1,
  output Y0
);

  wire one_all_add_1_co, one_all_add_2_co, one_all_add_3_co, one_all_add_4_co, one_all_add_5_co,
       one_all_add_6_co, one_all_add_7_co, one_all_add_8_co;

  one_all_add one_all_add_1 (.A(A0), .B(B0), .S(Y0), .CO(one_all_add_1_co));  // open: CI
  one_all_add one_all_add_2 (.CI(one_all_add_1_co), .A(A1), .B(B1), .S(Y1), .CO(one_all_add_2_co));
  one_all_add one_all_add_3 (.CI(one_all_add_2_co), .A(A2), .B(B2), .S(Y2), .CO(one_all_add_3_co));
  one_all_add one_all_add_4 (.CI(one_all_add_3_co), .A(A3), .B(B3), .S(Y3), .CO(one_all_add_4_co));
  one_all_add one_all_add_5 (.CI(one_all_add_4_co), .A(A4), .B(B4), .S(Y4), .CO(one_all_add_5_co));
  one_all_add one_all_add_6 (.CI(one_all_add_5_co), .A(A5), .B(B5), .S(Y5), .CO(one_all_add_6_co));
  one_all_add one_all_add_7 (.CI(one_all_add_6_co), .A(A6), .B(B6), .S(Y6), .CO(one_all_add_7_co));
  LED led_1 (.in(one_all_add_8_co));
  one_all_add one_all_add_8 (.CI(one_all_add_7_co), .A(A7), .B(B7), .S(Y7), .CO(one_all_add_8_co));

  // Notes on the sheet:
  //   8位加法器
  //   2个8位数求和
endmodule
