// Logisim project Sequential_logic_circuit.circ as structural Verilog
module SR_nor (
  input  R,
  input  S,
  output Q,
  output Q_bar
);

  nor nor_1 (Q, R, Q_bar);
  nor nor_2 (Q_bar, Q, S);

  // Notes on the sheet:
  //   或非门SR锁存器
endmodule

module SR_nand (
  input  R,
  input  S,
  output Q,
  output Q_bar
);

  nand nand_1 (Q, R, Q_bar);
  nand nand_2 (Q_bar, Q, S);

  // Notes on the sheet:
  //   与非门SR锁存器
endmodule

module D_latch (
  input  WE,
  input  D,
  output Q,
  output Q_bar
);

  wire and_1_out, and_2_out, not_1_out;

  not not_1 (not_1_out, D);
  and and_1 (and_1_out, D, WE);
  and and_2 (and_2_out, WE, not_1_out);
  SR_nor sr_nor_1 (.R(and_2_out), .S(and_1_out), .Q(Q), .Q_bar(Q_bar));

  // Notes on the sheet:
  //   D锁存器
endmodule

module D_latch_reset (
  input  WE,
  input  D,
  input  reset,
  output Q,
  output Q_bar
);

  wire and_1_out, and_2_out, and_3_out, not_1_out, not_2_out, or_1_out;

  not not_1 (not_1_out, D);
  and and_1 (and_1_out, D, WE);
  and and_2 (and_2_out, WE, not_1_out);
  not not_2 (not_2_out, reset);
  or or_1 (or_1_out, reset, and_2_out);
  and and_3 (and_3_out, and_1_out, not_2_out);
  SR_nor sr_nor_1 (.R(or_1_out), .S(and_3_out), .Q(Q), .Q_bar(Q_bar));

  // Notes on the sheet:
  //   带复位的D锁存器
endmodule

module D_latch_reset_return (
  input  in_1,
  input  in_2,
  input  in_3,
  output out_4,
  output out_5
);

  wire not_1_out;

  and and_1 (in_2, 1'b1, not_1_out);
  not not_1 (not_1_out, out_4);
  // D_latch_reset d_latch_reset_1: pin names not known; wires that end beside it: in_2, in_1, in_3, out_4, out_5

  // Notes on the sheet:
  //   带复位的D锁存器
endmodule

module DFF_reset (
  input  clk,
  input  D,
  input  reset,
  output out_4
);

  wire and_1_out, d_latch_1_q, not_1_out, not_2_out;

  not not_1 (not_1_out, reset);
  not not_2 (not_2_out, clk);
  and and_1 (and_1_out, D, not_1_out);
  D_latch d_latch_1 (.WE(not_2_out), .D(and_1_out), .Q(d_latch_1_q));  // open: Q_bar
  D_latch d_latch_2 (.WE(clk), .D(d_latch_1_q), .Q(out_4));  // open: Q_bar

  // Notes on the sheet:
  //   带复位功能的D触发器
endmodule

module DFF_return (
  input  clk,
  input  reset,
  output out_3
);

  wire and_1_out, d_latch_1_q, not_1_out, not_2_out, not_3_out;

  not not_1 (not_1_out, reset);
  not not_2 (not_2_out, clk);
  and and_1 (and_1_out, not_3_out, not_1_out);
  not not_3 (not_3_out, out_3);
  D_latch d_latch_1 (.WE(not_2_out), .D(and_1_out), .Q(d_latch_1_q));  // open: Q_bar
  D_latch d_latch_2 (.WE(clk), .D(d_latch_1_q), .Q(out_3));  // open: Q_bar
endmodule

module DFF_reset_we (
  input  clk,
  input  WE,
  input  D,
  input  reset,
  output Q,
  output Q_bar
);

  wire and_1_out, d_latch_1_q, not_1_out, not_2_out, one_two_one_1_y;

  and and_1 (and_1_out, D, not_1_out);
  not not_1 (not_1_out, reset);
  not not_2 (not_2_out, clk);
  one_two_one one_two_one_1 (.D1(Q), .S(WE), .D0(and_1_out), .Y(one_two_one_1_y));
  D_latch d_latch_1 (.WE(not_2_out), .D(one_two_one_1_y), .Q(d_latch_1_q));  // open: Q_bar
  D_latch d_latch_2 (.WE(clk), .D(d_latch_1_q), .Q(Q), .Q_bar(Q_bar));

  // Notes on the sheet:
  //   带WE的D触发器
endmodule

module DFF (
  input  clk,
  input  D,
  output Q,
  output Q_bar
);

  wire d_latch_1_q, not_1_out;

  not not_1 (not_1_out, clk);
  D_latch d_latch_1 (.WE(not_1_out), .D(D), .Q(d_latch_1_q));  // open: Q_bar
  D_latch d_latch_2 (.WE(clk), .D(d_latch_1_q), .Q(Q), .Q_bar(Q_bar));

  // Notes on the sheet:
  //   D触发器
endmodule

module register_4 (
  input  D3,
  input  D2,
  input  D1,
  input  D0,
  input  WE,
  input  clk,
  input  reset,
  output Q3,
  output Q2,
  output Q1,
  output Q0
);

  wire four_eight_decoder_16_to_light_1_ya, four_eight_decoder_16_to_light_1_yb,
       four_eight_decoder_16_to_light_1_yc, four_eight_decoder_16_to_light_1_yd,
       four_eight_decoder_16_to_light_1_ye, four_eight_decoder_16_to_light_1_yf,
       four_eight_decoder_16_to_light_1_yg;

  DFF_reset_we dff_reset_we_1 (.clk(clk), .WE(WE), .D(D0), .reset(reset), .Q(Q0));  // open: Q_bar
  DFF_reset_we dff_reset_we_2 (.clk(clk), .WE(WE), .D(D1), .reset(reset), .Q(Q1));  // open: Q_bar
  DFF_reset_we dff_reset_we_3 (.clk(clk), .WE(WE), .D(D2), .reset(reset), .Q(Q2));  // open: Q_bar
  DFF_reset_we dff_reset_we_4 (.clk(clk), .WE(WE), .D(D3), .reset(reset), .Q(Q3));  // open: Q_bar
  four_eight_decoder_16_to_light four_eight_decoder_16_to_light_1 (
    .A3(Q3), .A2(Q2), .A1(Q1), .A0(Q0), .S(1'b1), .Ye(four_eight_decoder_16_to_light_1_ye),
    .Yc(four_eight_decoder_16_to_light_1_yc), .Ya(four_eight_decoder_16_to_light_1_ya),
    .Yg(four_eight_decoder_16_to_light_1_yg), .Yf(four_eight_decoder_16_to_light_1_yf),
    .Yd(four_eight_decoder_16_to_light_1_yd), .Yb(four_eight_decoder_16_to_light_1_yb));
  _7_Segment_Display u_7_segment_display_1 (
    .g(four_eight_decoder_16_to_light_1_yg), .f(four_eight_decoder_16_to_light_1_yf),
    .a(four_eight_decoder_16_to_light_1_ya), .b(four_eight_decoder_16_to_light_1_yb),
    .e(four_eight_decoder_16_to_light_1_ye), .d(four_eight_decoder_16_to_light_1_yd),
    .c(four_eight_decoder_16_to_light_1_yc), .dp(1'b0));

  // Notes on the sheet:
  //   4位寄存器
endmodule

module counter_4 (
  input  WE,
  input  reset,
  output Q3,
  output Q2,
  output Q1,
  output Q0
);

  wire clk_out, D0, D1, D2, D3;

  Clock clk (.out(clk_out));
  register_4 register_4_1 (
    .D3(D3), .D2(D2), .D1(D1), .D0(D0), .WE(WE), .clk(clk_out), .reset(reset), .Q3(Q3), .Q2(Q2), .Q1(Q1),
    .Q0(Q0));
  main_four_add main_four_add_1 (
    .A3(Q3), .A2(Q2), .A1(Q1), .A0(Q0), .B3(1'b0), .B2(1'b0), .B1(1'b0), .B0(1'b1), .Y3(D3), .Y2(D2),
    .Y1(D1), .Y0(D0));  // open: CO

  // Notes on the sheet:
  //   4位计数器
endmodule

module register_8 (
  input  D7,
  input  D6,
  input  D5,
  input  D4,
  input  D3,
  input  D2,
  input  D1,
  input  D0,
  input  WE,
  input  clk,
  input  reset,
  output Q7,
  output Q6,
  output Q5,
  output Q4,
  output Q3,
  output Q2,
  output Q1,
  output Q0
);

  DFF_reset_we dff_reset_we_1 (.clk(clk), .WE(WE), .D(D0), .reset(reset), .Q(Q0));  // open: Q_bar
  DFF_reset_we dff_reset_we_2 (.clk(clk), .WE(WE), .D(D1), .reset(reset), .Q(Q1));  // open: Q_bar
  DFF_reset_we dff_reset_we_3 (.clk(clk), .WE(WE), .D(D2), .reset(reset), .Q(Q2));  // open: Q_bar
  DFF_reset_we dff_reset_we_4 (.clk(clk), .WE(WE), .D(D3), .reset(reset), .Q(Q3));  // open: Q_bar
  DFF_reset_we dff_reset_we_5 (.clk(clk), .WE(WE), .D(D4), .reset(reset), .Q(Q4));  // open: Q_bar
  DFF_reset_we dff_reset_we_6 (.clk(clk), .WE(WE), .D(D5), .reset(reset), .Q(Q5));  // open: Q_bar
  DFF_reset_we dff_reset_we_7 (.clk(clk), .WE(WE), .D(D6), .reset(reset), .Q(Q6));  // open: Q_bar
  DFF_reset_we dff_reset_we_8 (.clk(clk), .WE(WE), .D(D7), .reset(reset), .Q(Q7));  // open: Q_bar

  // Notes on the sheet:
  //   8位寄存器
endmodule

module add_total (
  input  reset,
  input  jie_chu_if,
  output Q7,
  output Q6,
  output Q5,
  output Q4,
  output Q3,
  output Q2,
  output Q1,
  output Q0
);

  wire clk, D0, D1, D2, D3, D4, D5, D6, D7, if_i_is_10_y, not_1_out, P0, P1, P2, P3, P4, P5, P6, P7, R0, R1,
       R2, R3, R4, R5, R6, R7, WE;

  Clock u_clk (.out(clk));
  eight_pk if_i_is_10 (
    .A7(P7), .A6(P6), .A5(P5), .A4(P4), .A3(P3), .A2(P2), .A1(P1), .A0(P0), .B7(1'b0), .B6(1'b0), .B5(1'b0),
    .B4(1'b0), .B3(1'b1), .B2(1'b0), .B1(1'b1), .B0(1'b1), .Y(if_i_is_10_y));
  not not_1 (not_1_out, jie_chu_if);
  and and_1 (WE, if_i_is_10_y, not_1_out);
  register_8 sum (
    .D7(R7), .D6(R6), .D5(R5), .D4(R4), .D3(R3), .D2(R2), .D1(R1), .D0(R0), .WE(WE), .clk(clk),
    .reset(reset), .Q7(Q7), .Q6(Q6), .Q5(Q5), .Q4(Q4), .Q3(Q3), .Q2(Q2), .Q1(Q1), .Q0(Q0));
  register_8 i (
    .D7(D7), .D6(D6), .D5(D5), .D4(D4), .D3(D3), .D2(D2), .D1(D1), .D0(D0), .WE(WE), .clk(clk),
    .reset(reset), .Q7(P7), .Q6(P6), .Q5(P5), .Q4(P4), .Q3(P3), .Q2(P2), .Q1(P1), .Q0(P0));
  eight_add sum_add_i (
    .B7(P7), .B6(P6), .B5(P5), .B4(P4), .B3(P3), .B2(P2), .B1(P1), .B0(P0), .A7(Q7), .A6(Q6), .A5(Q5),
    .A4(Q4), .A3(Q3), .A2(Q2), .A1(Q1), .A0(Q0), .Y7(R7), .Y6(R6), .Y5(R5), .Y4(R4), .Y3(R3), .Y2(R2),
    .Y1(R1), .Y0(R0));
  eight_add i_add_1 (
    .B7(1'b0), .B6(1'b0), .B5(1'b0), .B4(1'b0), .B3(1'b0), .B2(1'b0), .B1(1'b0), .B0(1'b1), .A7(P7), .A6(P6),
    .A5(P5), .A4(P4), .A3(P3), .A2(P2), .A1(P1), .A0(P0), .Y7(D7), .Y6(D6), .Y5(D5), .Y4(D4), .Y3(D3),
    .Y2(D2), .Y1(D1), .Y0(D0));

  // Other names for the same wires on the sheet: O = jie_chu_if
endmodule

module eight_pk (
  input  A7,
  input  A6,
  input  A5,
  input  A4,
  input  A3,
  input  A2,
  input  A1,
  input  A0,
  input  B7,
  input  B6,
  input  B5,
  input  B4,
  input  B3,
  input  B2,
  input  B1,
  input  B0,
  output Y
);

  wire xnor_1_out, xnor_2_out, xnor_3_out, xnor_4_out, xnor_5_out, xnor_6_out, xnor_7_out, xnor_8_out;

  xnor xnor_1 (xnor_1_out, A7, B7);
  xnor xnor_2 (xnor_2_out, A6, B6);
  xnor xnor_3 (xnor_3_out, A5, B5);
  xnor xnor_4 (xnor_4_out, A4, B4);
  xnor xnor_5 (xnor_5_out, A3, B3);
  xnor xnor_6 (xnor_6_out, A2, B2);
  xnor xnor_7 (xnor_7_out, A1, B1);
  xnor xnor_8 (xnor_8_out, A0, B0);
  and and_1 (Y, xnor_1_out, xnor_2_out, xnor_3_out, xnor_4_out, xnor_5_out, xnor_6_out, xnor_7_out, xnor_8_out);
endmodule

module digital_clock (
  input  WE,
  input  reset
);

  wire A0, A1, A2, A3, B0, B1, B2, B3, C0, C1, C2, C3, clk, D0, D1, D2, D3, E0, E1, E2, E3, F0, F1, F2, F3,
       four_eight_decoder_10_to_light_1_ya, four_eight_decoder_10_to_light_1_yb,
       four_eight_decoder_10_to_light_1_yc, four_eight_decoder_10_to_light_1_yd,
       four_eight_decoder_10_to_light_1_ye, four_eight_decoder_10_to_light_1_yf,
       four_eight_decoder_10_to_light_1_yg, four_eight_decoder_10_to_light_1_yh,
       four_eight_decoder_10_to_light_2_ya, four_eight_decoder_10_to_light_2_yb,
       four_eight_decoder_10_to_light_2_yc, four_eight_decoder_10_to_light_2_yd,
       four_eight_decoder_10_to_light_2_ye, four_eight_decoder_10_to_light_2_yf,
       four_eight_decoder_10_to_light_2_yg, four_eight_decoder_10_to_light_2_yh,
       four_eight_decoder_10_to_light_3_ya, four_eight_decoder_10_to_light_3_yb,
       four_eight_decoder_10_to_light_3_yc, four_eight_decoder_10_to_light_3_yd,
       four_eight_decoder_10_to_light_3_ye, four_eight_decoder_10_to_light_3_yf,
       four_eight_decoder_10_to_light_3_yg, four_eight_decoder_10_to_light_3_yh,
       four_eight_decoder_10_to_light_4_ya, four_eight_decoder_10_to_light_4_yb,
       four_eight_decoder_10_to_light_4_yc, four_eight_decoder_10_to_light_4_yd,
       four_eight_decoder_10_to_light_4_ye, four_eight_decoder_10_to_light_4_yf,
       four_eight_decoder_10_to_light_4_yg, four_eight_decoder_10_to_light_4_yh, G0, G1, G2, G3, H0, H1, H2,
       H3, or_1_out, or_2_out, or_3_out, or_4_out, Y0, Y1, Y2, Y3;

  Clock u_clk (.out(clk));
  or or_1 (or_1_out, reset, Y0);
  or or_2 (or_2_out, reset, Y1);
  or or_3 (or_3_out, reset, Y2);
  or or_4 (or_4_out, reset, Y3);
  register_4 sec_units (
    .D3(A3), .D2(A2), .D1(A1), .D0(A0), .WE(WE), .clk(clk), .reset(or_1_out), .Q3(B3), .Q2(B2), .Q1(B1),
    .Q0(B0));
  register_4 sec_tens (
    .D3(C3), .D2(C2), .D1(C1), .D0(C0), .WE(WE), .clk(clk), .reset(or_2_out), .Q3(D3), .Q2(D2), .Q1(D1),
    .Q0(D0));
  register_4 min_units (
    .D3(E3), .D2(E2), .D1(E1), .D0(E0), .WE(WE), .clk(clk), .reset(or_3_out), .Q3(F3), .Q2(F2), .Q1(F1),
    .Q0(F0));
  register_4 min_tens (
    .D3(G3), .D2(G2), .D1(G1), .D0(G0), .WE(WE), .clk(clk), .reset(or_4_out), .Q3(H3), .Q2(H2), .Q1(H1),
    .Q0(H0));
  main_four_add main_four_add_1 (
    .A3(B3), .A2(B2), .A1(B1), .A0(B0), .B3(1'b0), .B2(1'b0), .B1(1'b0), .B0(1'b1), .Y3(A3), .Y2(A2),
    .Y1(A1), .Y0(A0));  // open: CO
  main_four_add main_four_add_2 (
    .A3(D3), .A2(D2), .A1(D1), .A0(D0), .B3(1'b0), .B2(1'b0), .B1(1'b0), .B0(Y0), .Y3(C3), .Y2(C2), .Y1(C1),
    .Y0(C0));  // open: CO
  main_four_add main_four_add_3 (
    .A3(F3), .A2(F2), .A1(F1), .A0(F0), .B3(1'b0), .B2(1'b0), .B1(1'b0), .B0(Y1), .Y3(E3), .Y2(E2), .Y1(E1),
    .Y0(E0));  // open: CO
  main_four_add main_four_add_4 (
    .A3(H3), .A2(H2), .A1(H1), .A0(H0), .B3(1'b0), .B2(1'b0), .B1(1'b0), .B0(Y2), .Y3(G3), .Y2(G2), .Y1(G1),
    .Y0(G0));  // open: CO
  four_pk four_pk_1 (.A3(B3), .A2(B2), .A1(B1), .A0(B0), .B3(1'b1), .B2(1'b0), .B1(1'b0), .B0(1'b1), .Y(Y0));
  four_pk four_pk_2 (.A3(D3), .A2(D2), .A1(D1), .A0(D0), .B3(1'b0), .B2(1'b1), .B1(1'b1), .B0(1'b0), .Y(Y1));
  four_pk four_pk_3 (.A3(F3), .A2(F2), .A1(F1), .A0(F0), .B3(1'b1), .B2(1'b0), .B1(1'b0), .B0(1'b1), .Y(Y2));
  four_pk four_pk_4 (.A3(H3), .A2(H2), .A1(H1), .A0(H0), .B3(1'b0), .B2(1'b1), .B1(1'b1), .B0(1'b0), .Y(Y3));
  four_eight_decoder_10_to_light four_eight_decoder_10_to_light_1 (
    .A3(B3), .A2(B2), .A1(B1), .A0(B0), .Ya(four_eight_decoder_10_to_light_1_ya),
    .Yg(four_eight_decoder_10_to_light_1_yg), .Yd(four_eight_decoder_10_to_light_1_yd),
    .Yh(four_eight_decoder_10_to_light_1_yh), .Yb(four_eight_decoder_10_to_light_1_yb),
    .Ye(four_eight_decoder_10_to_light_1_ye), .Yf(four_eight_decoder_10_to_light_1_yf),
    .Yc(four_eight_decoder_10_to_light_1_yc));  // open: S
  four_eight_decoder_10_to_light four_eight_decoder_10_to_light_2 (
    .A3(D3), .A2(D2), .A1(D1), .A0(D0), .Ya(four_eight_decoder_10_to_light_2_ya),
    .Yg(four_eight_decoder_10_to_light_2_yg), .Yd(four_eight_decoder_10_to_light_2_yd),
    .Yh(four_eight_decoder_10_to_light_2_yh), .Yb(four_eight_decoder_10_to_light_2_yb),
    .Ye(four_eight_decoder_10_to_light_2_ye), .Yf(four_eight_decoder_10_to_light_2_yf),
    .Yc(four_eight_decoder_10_to_light_2_yc));  // open: S
  four_eight_decoder_10_to_light four_eight_decoder_10_to_light_3 (
    .A3(F3), .A2(F2), .A1(F1), .A0(F0), .Ya(four_eight_decoder_10_to_light_3_ya),
    .Yg(four_eight_decoder_10_to_light_3_yg), .Yd(four_eight_decoder_10_to_light_3_yd),
    .Yh(four_eight_decoder_10_to_light_3_yh), .Yb(four_eight_decoder_10_to_light_3_yb),
    .Ye(four_eight_decoder_10_to_light_3_ye), .Yf(four_eight_decoder_10_to_light_3_yf),
    .Yc(four_eight_decoder_10_to_light_3_yc));  // open: S
  four_eight_decoder_10_to_light four_eight_decoder_10_to_light_4 (
    .A3(H3), .A2(H2), .A1(H1), .A0(H0), .Ya(four_eight_decoder_10_to_light_4_ya),
    .Yg(four_eight_decoder_10_to_light_4_yg), .Yd(four_eight_decoder_10_to_light_4_yd),
    .Yh(four_eight_decoder_10_to_light_4_yh), .Yb(four_eight_decoder_10_to_light_4_yb),
    .Ye(four_eight_decoder_10_to_light_4_ye), .Yf(four_eight_decoder_10_to_light_4_yf),
    .Yc(four_eight_decoder_10_to_light_4_yc));  // open: S
  _7_Segment_Display u_7_segment_display_1 (
    .g(four_eight_decoder_10_to_light_1_yg), .f(four_eight_decoder_10_to_light_1_yf),
    .a(four_eight_decoder_10_to_light_1_ya), .b(four_eight_decoder_10_to_light_1_yb),
    .e(four_eight_decoder_10_to_light_1_ye), .d(four_eight_decoder_10_to_light_1_yd),
    .c(four_eight_decoder_10_to_light_1_yc), .dp(four_eight_decoder_10_to_light_1_yh));
  _7_Segment_Display u_7_segment_display_2 (
    .g(four_eight_decoder_10_to_light_2_yg), .f(four_eight_decoder_10_to_light_2_yf),
    .a(four_eight_decoder_10_to_light_2_ya), .b(four_eight_decoder_10_to_light_2_yb),
    .e(four_eight_decoder_10_to_light_2_ye), .d(four_eight_decoder_10_to_light_2_yd),
    .c(four_eight_decoder_10_to_light_2_yc), .dp(four_eight_decoder_10_to_light_2_yh));
  _7_Segment_Display u_7_segment_display_3 (
    .g(four_eight_decoder_10_to_light_3_yg), .f(four_eight_decoder_10_to_light_3_yf),
    .a(four_eight_decoder_10_to_light_3_ya), .b(four_eight_decoder_10_to_light_3_yb),
    .e(four_eight_decoder_10_to_light_3_ye), .d(four_eight_decoder_10_to_light_3_yd),
    .c(four_eight_decoder_10_to_light_3_yc), .dp(four_eight_decoder_10_to_light_3_yh));
  _7_Segment_Display u_7_segment_display_4 (
    .g(four_eight_decoder_10_to_light_4_yg), .f(four_eight_decoder_10_to_light_4_yf),
    .a(four_eight_decoder_10_to_light_4_ya), .b(four_eight_decoder_10_to_light_4_yb),
    .e(four_eight_decoder_10_to_light_4_ye), .d(four_eight_decoder_10_to_light_4_yd),
    .c(four_eight_decoder_10_to_light_4_yc), .dp(four_eight_decoder_10_to_light_4_yh));
endmodule

module four_pk (
  input  A3,
  input  A2,
  input  A1,
  input  A0,
  input  B3,
  input  B2,
  input  B1,
  input  B0,
  output Y
);

  wire xnor_1_out, xnor_2_out, xnor_3_out, xnor_4_out;

  xnor xnor_1 (xnor_1_out, A3, B3);
  xnor xnor_2 (xnor_2_out, A2, B2);
  xnor xnor_3 (xnor_3_out, A1, B1);
  xnor xnor_4 (xnor_4_out, A0, B0);
  and and_1 (Y, xnor_1_out, xnor_2_out, xnor_3_out, xnor_4_out);
endmodule
