// Logisim project OR_MOS.circ as structural Verilog: 1 circuit, main circuit main
module main (
  input  A,
  input  B,
  output Y
);

  wire transistor_1_out, transistor_3_out;

  Transistor #(.\type ("n")) transistor_1 (.in(1'b0), .out(transistor_1_out), .gate(A));
  Transistor #(.\type ("n")) transistor_2 (.in(1'b0), .out(transistor_1_out), .gate(B));
  Transistor transistor_3 (.in(1'b1), .out(transistor_3_out), .gate(A));
  Transistor transistor_4 (.in(transistor_3_out), .out(transistor_1_out), .gate(B));
  Transistor transistor_5 (.in(1'b1), .out(Y), .gate(transistor_1_out));
  Transistor #(.\type ("n")) transistor_6 (.in(1'b0), .out(Y), .gate(transistor_1_out));

  // Notes on the sheet:
  //   或门OR
endmodule
