// Logisim project SELF_74HC138.circ as structural Verilog: 1 circuit, main circuit main
module main (
  input  S1,
  input  S2_bar,
  input  S3_bar,
  input  A0,
  input  A1,
  input  A2,
  output Y0_bar,
  output Y1_bar,
  output Y2_bar,
  output Y3_bar,
  output Y4_bar,
  output Y5_bar,
  output Y6_bar,
  output Y7_bar
);

  wire GS_out, not_1_out, not_2_out, not_3_out, not_4_out, not_5_out, not_6_out, not_7_out;

  not not_1 (not_1_out, S1);
  and GS (GS_out, ~not_1_out, ~S2_bar, ~S3_bar);  // AND_Gate
  not not_2 (not_2_out, A0);
  not not_3 (not_3_out, A1);
  not not_4 (not_4_out, A2);
  not not_5 (not_5_out, not_2_out);
  not not_6 (not_6_out, not_3_out);
  not not_7 (not_7_out, not_4_out);
  nand G0 (Y0_bar, not_2_out, not_3_out, not_4_out, GS_out);
  nand G1 (Y1_bar, not_5_out, not_3_out, not_4_out, GS_out);
  nand G2 (Y2_bar, not_2_out, not_6_out, not_4_out, GS_out);
  nand G3 (Y3_bar, not_5_out, not_6_out, not_4_out, GS_out);
  nand G4 (Y4_bar, not_2_out, not_3_out, not_7_out, GS_out);
  nand G5 (Y5_bar, not_3_out, not_7_out, not_5_out, GS_out);
  nand G6 (Y6_bar, not_2_out, not_7_out, not_6_out, GS_out);
  nand G7 (Y7_bar, GS_out, not_6_out, not_5_out, not_7_out);

  // Notes on the sheet:
  //   74HC138
endmodule
