// Logisim project XNOR_TOTAL.circ as structural Verilog: 1 circuit, main circuit main
module main (
  input  A1,
  input  B1,
  input  A2,
  input  B2,
  output Y1,
  output Y2
);

  wire and_1_out, and_2_out, transistor_1_out;

  Transistor transistor_1 (.in(1'b1), .out(transistor_1_out), .gate(A2));
  Transistor #(.\type ("n")) transistor_2 (.in(1'b0), .out(transistor_1_out), .gate(A2));
  and and_1 (and_1_out, A1, B1);
  and and_2 (and_2_out, ~B1, ~A1);  // AND_Gate
  Transistor #(.\type ("n")) transistor_3 (.in(A2), .out(Y2), .gate(B2));
  Transistor transistor_4 (.in(transistor_1_out), .out(Y2), .gate(B2));
  or or_1 (Y1, and_1_out, and_2_out);
  Transistor #(.\type ("n")) transistor_5 (.in(B2), .out(Y2), .gate(A2));
  Transistor transistor_6 (.in(B2), .out(Y2), .gate(transistor_1_out));

  // Other names for the same wires on the sheet: B = B2

  // Notes on the sheet:
  //   XNOR
endmodule
