// Logisim project XOR_TOTAL.circ as structural Verilog: 1 circuit, main circuit main
module main (
  input  in_1,
  input  in_2,
  input  A,
  input  in_4,
  input  in_5,
  input  B,
  input  in_7,
  input  in_8,
  output out_9,
  output Y,
  output out_11,
  output out_12
);

  wire and_1_out, and_2_out, and_3_out, nand_1_out, nand_2_out, nand_3_out, nor_1_out, not_1_out, not_2_out,
       transistor_1_out;

  not not_1 (not_1_out, in_2);
  not not_2 (not_2_out, in_1);
  and and_1 (and_1_out, in_1, not_1_out);
  and and_2 (and_2_out, in_2, not_2_out);
  nand nand_1 (nand_1_out, in_4, in_5);
  nor nor_1 (nor_1_out, in_7, in_8);
  and and_3 (and_3_out, in_7, in_8);
  or or_1 (out_9, and_1_out, and_2_out);
  nand nand_2 (nand_2_out, nand_1_out, in_4);
  nand nand_3 (nand_3_out, nand_1_out, in_5);
  nand nand_4 (out_11, nand_2_out, nand_3_out);
  nor nor_2 (out_12, nor_1_out, and_3_out);
  Transistor transistor_1 (.in(1'b1), .out(transistor_1_out), .gate(A));
  Transistor #(.\type ("n")) transistor_2 (.in(1'b0), .out(transistor_1_out), .gate(A));
  Transistor transistor_3 (.in(A), .out(Y), .gate(B));
  Transistor #(.\type ("n")) transistor_4 (.in(transistor_1_out), .out(Y), .gate(B));
  Transistor transistor_5 (.in(B), .out(Y), .gate(A));
  Transistor #(.\type ("n")) transistor_6 (.in(B), .out(Y), .gate(transistor_1_out));

  // Notes on the sheet:
  //   异或门
  //   16MOS方案
  //   14MOS方案
  //   XOR全定制
endmodule
