// Logisim project Num_four_seven.circ as structural Verilog: 2 circuits, main circuit main
module main (
  input  A3,
  input  A2,
  input  A1,
  input  A0
);

  wire four_to_eight_1_ya, four_to_eight_1_yb, four_to_eight_1_yc, four_to_eight_1_yd, four_to_eight_1_ye,
       four_to_eight_1_yf, four_to_eight_1_yg;

  four_to_eight four_to_eight_1 (
    .A3(A3), .A2(A2), .A1(A1), .A0(A0), .Ye(four_to_eight_1_ye), .Ya(four_to_eight_1_ya),
    .Yf(four_to_eight_1_yf), .Yb(four_to_eight_1_yb), .Yg(four_to_eight_1_yg), .Yc(four_to_eight_1_yc),
    .Yd(four_to_eight_1_yd));
  _7_Segment_Display u_7_segment_display_1 (
    .g(four_to_eight_1_yg), .f(four_to_eight_1_yf), .a(four_to_eight_1_ya), .b(four_to_eight_1_yb),
    .e(four_to_eight_1_ye), .d(four_to_eight_1_yd), .c(four_to_eight_1_yc));  // open: dp
endmodule

module four_to_eight (
  input  A3,
  input  A2,
  input  A1,
  input  A0,
  output Ye,
  output Ya,
  output Yf,
  output Yb,
  output Yg,
  output Yc,
  output Yd
);

  wire and_1_out, and_2_out, and_3_out, and_4_out, and_5_out, and_6_out, and_7_out, and_8_out, and_9_out,
       and_10_out, and_11_out, and_12_out, and_13_out, and_14_out, and_15_out, and_16_out, and_17_out;

  and and_1 (and_1_out, ~A3, ~A2, ~A1, A0);  // AND_Gate
  and and_2 (and_2_out, A3, A1);
  and and_3 (and_3_out, A2, ~A0);  // AND_Gate
  and and_4 (and_4_out, A3, A1);
  and and_5 (and_5_out, A2, A1, ~A0);  // AND_Gate
  and and_6 (and_6_out, A2, ~A1, A0);  // AND_Gate
  and and_7 (and_7_out, A3, A2);
  and and_8 (and_8_out, ~A2, A1, ~A0);  // AND_Gate
  and and_9 (and_9_out, A2, A1, A0);
  and and_10 (and_10_out, A2, ~A1, ~A0);  // AND_Gate
  and and_11 (and_11_out, ~A2, ~A1, A0);  // AND_Gate
  nor nor_1 (Ya, and_1_out, and_2_out, and_3_out);
  nor nor_2 (Yb, and_4_out, and_5_out, and_6_out);
  nor nor_3 (Yc, and_7_out, and_8_out);
  nor nor_4 (Yd, and_9_out, and_10_out, and_11_out);
  and and_12 (and_12_out, A2, ~A1);  // AND_Gate
  and and_13 (and_13_out, ~A3, ~A2, A0);  // AND_Gate
  and and_14 (and_14_out, ~A2, A1);  // AND_Gate
  and and_15 (and_15_out, A1, A0);
  and and_16 (and_16_out, ~A3, ~A2, ~A1);  // AND_Gate
  and and_17 (and_17_out, A2, A1, A0);
  nor nor_5 (Ye, and_12_out, A0);
  nor nor_6 (Yf, and_13_out, and_14_out, and_15_out);
  nor nor_7 (Yg, and_16_out, and_17_out);

  // Notes on the sheet:
  //   四输入七输出（每个输出控制一个灯）
endmodule
