// Logisim project minirv_m.circ as structural Verilog: 3 circuits, main circuit main
module main (
);

  wire and_11_out, and_12_out, and_13_out, and_14_out, and_15_out, be0, be1, be2, be3, clk, comparator_1_eq,
       comparator_1_gt, comparator_2_lt, comparator_3_eq, comparator_4_eq, comparator_5_eq, comparator_6_eq,
       comparator_7_eq, comparator_9_eq, comparator_10_eq, comparator_11_eq, comparator_12_eq,
       comparator_13_eq, comparator_14_eq, comparator_15_eq, decoder_1_out0, decoder_1_out1, decoder_1_out2,
       decoder_1_out3, is_add, is_addi, is_jalr, is_lbu, is_lbu_lw, is_lbu_sb, is_lui, is_lw, is_MEM, is_sb,
       is_sw, is_sw_sb, is_VGA, or_1_out, R, RegWrite, rgb_video_1_p3;
  wire [2:0] funct3;
  wire [3:0] rd, rs1, rs2;
  wire [6:0] opcode;
  wire [7:0] lbu_data, X, Y;
  wire [31:0] addi_jalr_lw_lbu_imm, alu_result, and_1_out, Back, lui_imm, lw_data, multiplexer_1_out,
       multiplexer_2_out, multiplexer_3_out, multiplexer_4_out, multiplexer_6_out, multiplexer_9_out,
       next_seq_PC, o_imm_32, o_PC, rdata1, rdata2, rom_1_data, subtractor_1_out, sw_sb_imm, wdata;
  wire [31:16] shifter_1_out;

  Clock clock_1 (.out(clk));
  Button button_1 (.out(R));
  Adder #(.width(32)) adder_1 (.a(o_PC), .b(32'h4), .out(next_seq_PC));  // open: cin, cout
  assign and_1_out = alu_result & 32'hfffffffe;  // AND_Gate and_1, 32 bits wide
  Multiplexer #(.width(32)) multiplexer_1 (.in0(rdata1), .in1({32{1'b0}}), .out(multiplexer_1_out), .sel(is_lui));
  Multiplexer #(.width(32)) multiplexer_2 (.in0(o_imm_32), .in1(rdata2), .out(multiplexer_2_out), .sel(is_add));
  Multiplexer #(.width(32)) multiplexer_3 (.in0(next_seq_PC), .in1(and_1_out), .out(multiplexer_3_out), .sel(is_jalr));
  Adder #(.width(32)) adder_2 (.a(multiplexer_1_out), .b(multiplexer_2_out), .out(alu_result));  // open: cin, cout
  Multiplexer #(.width(32)) multiplexer_4 (
    .in0(addi_jalr_lw_lbu_imm), .in1(lui_imm), .out(multiplexer_4_out), .sel(is_lui));
  Comparator #(.width(32)) comparator_1 (
    .a(alu_result), .b(32'h20000000), .gt(comparator_1_gt), .eq(comparator_1_eq));  // open: lt
  Comparator #(.width(32)) comparator_2 (.a(alu_result), .b(32'h20040000), .lt(comparator_2_lt));  // open: gt, eq
  Subtractor #(.width(32)) subtractor_1 (
    .a(alu_result), .b(32'h20000000), .out(subtractor_1_out), .bin(1'b0));  // open: bout
  Register #(.width(32)) PC (.D(multiplexer_3_out), .en(1'b1), .clk(clk), .Q(o_PC), .clr(R));
  Multiplexer #(.width(32)) multiplexer_5 (.in0(multiplexer_4_out), .in1(sw_sb_imm), .out(o_imm_32), .sel(is_sw_sb));
  or or_1 (or_1_out, comparator_1_gt, comparator_1_eq);
  and and_2 (is_VGA, or_1_out, comparator_2_lt);
  Shifter #(.shift("lr"), .width(32)) shifter_1 (.in(subtractor_1_out), .\dist (5'b00010), .out({shifter_1_out, Y, X}));
  GPR gpr_1 (
    .wdata(wdata), .rd(rd), .WE(RegWrite), .clk(clk), .R(R), .rs1(rs1), .rs2(rs2), .rdata1(rdata1),
    .rdata2(rdata2));
  Multiplexer #(.width(32)) multiplexer_6 (
    .in0(lw_data), .in1({{24{1'b0}}, lbu_data}), .out(multiplexer_6_out), .sel(is_lbu));
  not not_1 (is_MEM, is_VGA);
  Multiplexer #(.width(32)) multiplexer_7 (.in0(alu_result), .in1(multiplexer_6_out), .out(Back), .sel(is_lbu_lw));
  ROM #(.addrWidth(24), .dataWidth(32)) rom_1 (.addr(o_PC[25:2]), .data(rom_1_data));
  Multiplexer #(.width(32)) multiplexer_8 (.in0(Back), .in1(next_seq_PC), .out(wdata), .sel(is_jalr));
  // RGB_Video #(.cursor("No Cursor"), .height(256), .scale(1), .width(256)) rgb_video_1: pin names not known; wires that end beside it: R, clk, rgb_video_1_p3, X, Y, rdata2[23:0]
  and and_3 (rgb_video_1_p3, is_VGA, is_sw);
  Comparator #(.width(7)) comparator_3 (.a(opcode), .b(7'b0010011), .eq(comparator_3_eq));  // open: gt, lt
  and and_4 (is_addi, comparator_3_eq, comparator_4_eq);
  Comparator #(.width(3)) comparator_4 (.a(funct3), .b(3'b000), .eq(comparator_4_eq));  // open: gt, lt
  and and_5 (is_jalr, comparator_4_eq, comparator_5_eq);
  Comparator #(.width(7)) comparator_5 (.a(opcode), .b(7'b1100111), .eq(comparator_5_eq));  // open: gt, lt
  Comparator #(.width(7)) comparator_6 (.a(opcode), .b(7'b0110011), .eq(comparator_6_eq));  // open: gt, lt
  and and_6 (is_add, comparator_6_eq, comparator_7_eq);
  Comparator #(.width(3)) comparator_7 (.a(funct3), .b(3'b000), .eq(comparator_7_eq));  // open: gt, lt
  Comparator #(.width(7)) comparator_8 (.a(opcode), .b(7'b0110111), .eq(is_lui));  // open: gt, lt
  Comparator #(.width(7)) comparator_9 (.a(opcode), .b(7'b0000011), .eq(comparator_9_eq));  // open: gt, lt
  and and_7 (is_lw, comparator_9_eq, comparator_10_eq);
  Comparator #(.width(3)) comparator_10 (.a(funct3), .b(3'b010), .eq(comparator_10_eq));  // open: gt, lt
  and and_8 (is_sw, comparator_10_eq, comparator_11_eq);
  Comparator #(.width(7)) comparator_11 (.a(opcode), .b(7'b0100011), .eq(comparator_11_eq));  // open: gt, lt
  Comparator #(.width(7)) comparator_12 (.a(opcode), .b(7'b0000011), .eq(comparator_12_eq));  // open: gt, lt
  and and_9 (is_lbu, comparator_12_eq, comparator_13_eq);
  Comparator #(.width(3)) comparator_13 (.a(funct3), .b(3'b100), .eq(comparator_13_eq));  // open: gt, lt
  Comparator #(.width(7)) comparator_14 (.a(opcode), .b(7'b0100011), .eq(comparator_14_eq));  // open: gt, lt
  and and_10 (is_sb, comparator_14_eq, comparator_15_eq);
  Comparator #(.width(3)) comparator_15 (.a(funct3), .b(3'b000), .eq(comparator_15_eq));  // open: gt, lt
  inst_decoder inst_decoder_1 (
    .instruction(rom_1_data), .opcode(opcode), .funct3(funct3), .rd(rd), .rs1(rs1), .rs2(rs2),
    .sw_sb_imm(sw_sb_imm), .addi_jalr_lw_lbu_imm(addi_jalr_lw_lbu_imm), .lui_imm(lui_imm));
  Decoder #(.select(2)) decoder_1 (
    .out0(decoder_1_out0), .out1(decoder_1_out1), .out2(decoder_1_out2), .out3(decoder_1_out3),
    .sel(alu_result[1:0]));  // open: en
  and and_11 (and_11_out, decoder_1_out3, is_lbu_sb);
  and and_12 (and_12_out, decoder_1_out2, is_lbu_sb);
  and and_13 (and_13_out, decoder_1_out1, is_lbu_sb);
  and and_14 (and_14_out, decoder_1_out0, is_lbu_sb);
  or or_2 (RegWrite, is_addi, is_jalr, is_lw, is_add, is_lui, is_lbu);
  or or_3 (is_sw_sb, is_sw, is_sb);
  or or_4 (is_lbu_sb, is_sb, is_lbu);
  or or_5 (is_lbu_lw, is_lbu, is_lw);
  and and_15 (and_15_out, is_sw_sb, is_MEM);
  or or_6 (be3, is_sw, and_11_out);
  or or_7 (be2, is_sw, and_12_out);
  or or_8 (be1, is_sw, and_13_out);
  or or_9 (be0, is_sw, and_14_out);
  RAM #(.addrWidth(24), .asyncread("true"), .byteenables("byteEnables"), .dataWidth(32), .\type ("nonvolatile")) ram_1 (
    .addr(alu_result[25:2]), .we(and_15_out), .oe(1'b1), .clk(clk), .din(multiplexer_9_out), .dout(lw_data),
    .be3(be3), .be2(be2), .be1(be1), .be0(be0));
  Multiplexer #(.width(32)) multiplexer_9 (
    .in0(rdata2), .in1({rdata2[7:0], rdata2[7:0], rdata2[7:0], rdata2[7:0]}), .out(multiplexer_9_out),
    .sel(is_sb));
  Multiplexer #(.select(2), .width(8)) multiplexer_10 (
    .in0(lw_data[7:0]), .in1(lw_data[15:8]), .in2(lw_data[23:16]), .in3(lw_data[31:24]), .out(lbu_data),
    .sel(alu_result[1:0]));

  // Other names for the same wires on the sheet: to_be[1:0] = alu_result[1:0]; ALUResult_24[23:0] = alu_result[25:2]

  // Notes on the sheet:
  //   contents of rom_1 (hex, n*v repeats v):
  //   413 93137 10113 10b7 dbc08093 80e7 fe012823 fea10923 fea12423 fe914203 fe4109a3 ff012783 f787b3
  //   f787b3 4b6b7 f0068693 fdc10113 d787b3 10000713 f12423 10593 100793 b00513 2112023 12023 12223 e12623
  //   e12823 f10a23 10b7 a8408093 80e7 2012083 2410113 8067 ff410113 112423 10b7 a7c08093 80e7 513 1800093
  //   80e7 812083 513 c10113 8067 852583 feb12823 fe812e23 3437 a0840413 ff014183 3401b3 1c183 ff114203
  //   440233 24203 4181b3 ff214203 440233 24203 4181b3 ff314203 440233 24203 4181b3 3237 a0020213 320233
  //   24203 ffc12403 420233 420233 410233 11b7 85c18193 fe312823 14800193 fe312623 fec22203 20067 1052703
  //   52683 452783 fe810113 e12423 112a23 fed12823 fef12623 13737 c0070713 fe012223 ff314203 fe4102a3
  //   fef14203 fe410223 fe412203 470233 24203 fe4105a3 ff214203 fe4102a3 fee14203 fe410223 fe412203 470233
  //   24203 fe410523 ff114203 fe4102a3 fed14203 fe410223 fe412203 470233 24203 fe4104a3 ff014203 fe4102a3
  //   fec14203 fe410223 fe412203 470233 24203 fe410423 fe812703 c52603 fee12823 fe812e23 3437 a0840413
  //   ff014183 3401b3 1c183 ff114203 440233 24203 4181b3 ff214203 440233 24203 4181b3 ff314203 440233
  //   24203 4181b3 3237 a0020213 320233 24203 ffc12403 420233 420233 410233 66800193 fe312823 28000193
  //   fe312623 fec22203 20067 c68733 10000513 fe812e23 fe912c23 fee12823 50413 ff012483 fe812423 feb14183
  //   3181b3 fe312423 fe914183 3181b3 fe912423 feb14203 420233 fe412423 fe914203 4181b3 3181b3 fe312a23
  //   fe912423 33237 b0020213 feb14183 4181b3 1c183 fe3103a3 fea14183 4181b3 1c183 fe310323 fe914183
  //   4181b3 1c183 fe3102a3 fe814183 4181b3 1c183 fe310223 ff412183 fe412203 440233 120213 fe412423
  //   feb14203 420233 fe412423 fe914203 4181b3 3237 b0820213 320233 ff812483 ffc12403 24203 420233 420233
  //   410233 11b7 86018193 fe312823 38800193 fe312623 fec22203 20067 812703 10000513 812823 e78733
  //   fe812e23 fe912c23 fee12823 50413 ff012483 fe812423 feb14183 3181b3 fe312423 fe914183 3181b3 fe912423
  //   feb14203 420233 fe412423 fe914203 4181b3 3181b3 fe312a23 fe912423 33237 b0020213 feb14183 4181b3
  //   1c183 fe3103a3 fea14183 4181b3 1c183 fe310323 fe914183 4181b3 1c183 fe3102a3 fe814183 4181b3 1c183
  //   fe310223 ff412183 fe412203 440233 120213 fe412423 feb14203 420233 fe412423 fe914203 4181b3 3237
  //   b0820213 320233 ff812483 ffc12403 24203 420233 420233 410233 11b7 86418193 fe312823 49800193
  //   fe312623 fec22203 20067 8*f787b3 d787b3 f787b3 f787b3 20000437 f40433 812783 c60633 c60633 fef12423
  //   feb14183 3181b3 fe312423 fe914183 fff78213 fe412423 feb14203 420233 fe412423 fe914203 4181b3 3237
  //   b1820213 418233 24203 420233 420233 410233 65800193 fe312823 53c00193 fe312623 fec22203 20067 912623
  //   493 40513 c12223 b12023 10b7 de008093 80e7 12583 412603 812783 148493 40040413 c585b3 fef12823
  //   fe912623 fe812e23 fe912c23 4b437 d0040413 ff014183 340233 100193 320023 fec14183 3401b3 18023 24183
  //   ff114483 940233 100493 920023 fed14483 9404b3 48023 24483 9181b3 ff214483 940233 100493 920023
  //   fee14483 9404b3 48023 24483 9181b3 ff314483 940233 100493 920023 fef14483 9404b3 48023 24483 9181b3
  //   3237 a0020213 320233 24203 ff812483 ffc12403 420233 420233 410233 65400193 fe312823 54400193
  //   fe312623 fec22203 20067 c12483 1012403 1412083 1810113 8067 10000713 fec12823 fee12623 fe812e23
  //   fe912c23 4b437 d0040413 ff014183 340233 100193 320023 fec14183 3401b3 18023 24183 ff114483 940233
  //   100493 920023 fed14483 9404b3 48023 24483 9181b3 ff214483 940233 100493 920023 fee14483 9404b3 48023
  //   24483 9181b3 ff314483 940233 100493 920023 fef14483 9404b3 48023 24483 9181b3 3237 a0020213 320233
  //   24203 ff812483 ffc12403 420233 420233 410233 74c00193 fe312823 28000193 fe312623 fec22203 20067
  //   812703 fee12823 fec12623 fe812e23 fe912c23 4b437 d0040413 ff014183 340233 100193 320023 fec14183
  //   3401b3 18023 24183 ff114483 940233 100493 920023 fed14483 9404b3 48023 24483 9181b3 ff214483 940233
  //   100493 920023 fee14483 9404b3 48023 24483 9181b3 ff314483 940233 100493 920023 fef14483 9404b3 48023
  //   24483 9181b3 3237 a0020213 320233 24203 ff812483 ffc12403 420233 420233 410233 11b7 83418193
  //   fe312823 38800193 fe312623 fec22203 20067 1412083 40637 20000537 1810113 1237 de020213 20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
endmodule

module GPR (
  input  [31:0] wdata,
  input  [3:0] rd,
  input  WE,
  input  clk,
  input  R,
  input  [3:0] rs1,
  input  [3:0] rs2,
  output [31:0] rdata1,
  output [31:0] rdata2
);

  wire decoder_1_out1, decoder_1_out2, decoder_1_out3, decoder_1_out4, decoder_1_out5, decoder_1_out6,
       decoder_1_out7, decoder_1_out8, decoder_1_out9, decoder_1_out10, decoder_1_out11, decoder_1_out12,
       decoder_1_out13, decoder_1_out14, decoder_1_out15;
  wire [31:0] register_1_q, register_2_q, register_3_q, register_4_q, register_5_q, register_6_q,
       register_7_q, register_8_q, register_9_q, register_10_q, register_11_q, register_12_q, register_13_q,
       register_14_q, register_15_q, register_16_q;

  Decoder #(.select(4)) decoder_1 (
    .out1(decoder_1_out1), .out2(decoder_1_out2), .out3(decoder_1_out3), .out4(decoder_1_out4),
    .out5(decoder_1_out5), .out6(decoder_1_out6), .out7(decoder_1_out7), .out8(decoder_1_out8),
    .out9(decoder_1_out9), .out10(decoder_1_out10), .out11(decoder_1_out11), .out12(decoder_1_out12),
    .out13(decoder_1_out13), .out14(decoder_1_out14), .out15(decoder_1_out15), .sel(rd), .en(WE));  // open: out0
  Register #(.width(32)) register_1 (.D(wdata), .en(1'b0), .clk(clk), .Q(register_1_q), .clr(R));
  Register #(.width(32)) register_2 (.D(wdata), .en(decoder_1_out8), .clk(clk), .Q(register_2_q), .clr(R));
  Register #(.width(32)) register_3 (.D(wdata), .en(decoder_1_out1), .clk(clk), .Q(register_3_q), .clr(R));
  Register #(.width(32)) register_4 (.D(wdata), .en(decoder_1_out9), .clk(clk), .Q(register_4_q), .clr(R));
  Register #(.width(32)) register_5 (.D(wdata), .en(decoder_1_out2), .clk(clk), .Q(register_5_q), .clr(R));
  Register #(.width(32)) register_6 (.D(wdata), .en(decoder_1_out10), .clk(clk), .Q(register_6_q), .clr(R));
  Register #(.width(32)) register_7 (.D(wdata), .en(decoder_1_out3), .clk(clk), .Q(register_7_q), .clr(R));
  Register #(.width(32)) register_8 (.D(wdata), .en(decoder_1_out11), .clk(clk), .Q(register_8_q), .clr(R));
  Register #(.width(32)) register_9 (.D(wdata), .en(decoder_1_out4), .clk(clk), .Q(register_9_q), .clr(R));
  Register #(.width(32)) register_10 (.D(wdata), .en(decoder_1_out12), .clk(clk), .Q(register_10_q), .clr(R));
  Register #(.width(32)) register_11 (.D(wdata), .en(decoder_1_out5), .clk(clk), .Q(register_11_q), .clr(R));
  Register #(.width(32)) register_12 (.D(wdata), .en(decoder_1_out13), .clk(clk), .Q(register_12_q), .clr(R));
  Register #(.width(32)) register_13 (.D(wdata), .en(decoder_1_out6), .clk(clk), .Q(register_13_q), .clr(R));
  Register #(.width(32)) register_14 (.D(wdata), .en(decoder_1_out14), .clk(clk), .Q(register_14_q), .clr(R));
  Register #(.width(32)) register_15 (.D(wdata), .en(decoder_1_out7), .clk(clk), .Q(register_15_q), .clr(R));
  Register #(.width(32)) register_16 (.D(wdata), .en(decoder_1_out15), .clk(clk), .Q(register_16_q), .clr(R));
  // Probe on register_1_q
  // Probe on register_3_q
  // Probe on register_5_q
  // Probe on register_7_q
  // Probe on register_9_q
  // Probe on register_11_q
  // Probe on register_13_q
  // Probe on register_15_q
  // Probe on register_2_q
  // Probe on register_4_q
  // Probe on register_6_q
  // Probe on register_8_q
  // Probe on register_10_q
  // Probe on register_12_q
  // Probe on register_14_q
  // Probe on register_16_q
  Multiplexer #(.select(4), .width(32)) multiplexer_1 (
    .in0(register_1_q), .in1(register_3_q), .in2(register_5_q), .in3(register_7_q), .in4(register_9_q),
    .in5(register_11_q), .in6(register_13_q), .in7(register_15_q), .in8(register_2_q), .in9(register_4_q),
    .in10(register_6_q), .in11(register_8_q), .in12(register_10_q), .in13(register_12_q),
    .in14(register_14_q), .in15(register_16_q), .out(rdata1), .sel(rs1));
  Multiplexer #(.select(4), .width(32)) multiplexer_2 (
    .in0(register_1_q), .in1(register_3_q), .in2(register_5_q), .in3(register_7_q), .in4(register_9_q),
    .in5(register_11_q), .in6(register_13_q), .in7(register_15_q), .in8(register_2_q), .in9(register_4_q),
    .in10(register_6_q), .in11(register_8_q), .in12(register_10_q), .in13(register_12_q),
    .in14(register_14_q), .in15(register_16_q), .out(rdata2), .sel(rs2));

  // Notes on the sheet:
  //   x0
  //   x1
  //   x2
  //   x3
  //   x4
  //   x5
  //   x6
  //   x7
  //   x8
  //   x9
  //   x10
  //   x11
  //   x12
  //   x13
  //   x14
  //   x15
endmodule

module inst_decoder (
  input  [31:0] instruction,
  output [6:0] opcode,
  output [2:0] funct3,
  output [3:0] rd,
  output [3:0] rs1,
  output [3:0] rs2,
  output [31:0] sw_sb_imm,
  output [31:0] addi_jalr_lw_lbu_imm,
  output [31:0] lui_imm
);

  assign sw_sb_imm = {{20{instruction[31]}}, {instruction[31:25], instruction[11:7]}};  // Bit_Extender bit_extender_1
  assign addi_jalr_lw_lbu_imm = {{20{instruction[31]}}, instruction[31:20]};  // Bit_Extender bit_extender_2

  assign funct3 = instruction[14:12];
  assign lui_imm = {instruction[31:12], {12{1'b0}}};
  assign opcode = instruction[6:0];
  assign rd = instruction[10:7];
  assign rs1 = instruction[18:15];
  assign rs2 = instruction[23:20];
endmodule
