// Logisim project sCPU.circ as structural Verilog: 7 circuits, main circuit main
module main (
  input  WE
);

  wire add_WE, bner0_WE, clk, comparator_1_eq, CP, li_WE, multiplexer_1_out, not_9_out, not_13_out,
       not_14_out, out_WE, RST, transmission_7_p3, transmission_8_p3, transmission_10_p3;
  wire [1:0] opcode, rd, rdout, rs1, rs2, transmission_1_p2, transmission_4_p3, transmission_5_p3;
  wire [3:0] ADDR, addr_t, imm, pc_4bit_1_output_addr;
  wire [7:0] Dout, Dout1, Dout2, outline, rd0, rd1, rd2, rd3, rom_8_1_instruction, transmission_2_p2,
       transmission_10_p4, transmission_11_p3;

  Button button_1 (.out(RST));
  Button button_2 (.out(clk));
  // Transmission_Gate #(.width(2)) transmission_1: pin names not known; wires that end beside it: rdout, transmission_1_p2
  // NOT_Gate not_1 has open pins: in=out_WE, out=open
  // Transmission_Gate #(.width(8)) transmission_2: pin names not known; wires that end beside it: {4'b0000, imm}, transmission_2_p2
  // NOT_Gate not_2 has open pins: in=li_WE, out=open
  // Transmission_Gate #(.width(2)) transmission_3: pin names not known; wires that end beside it: rd, li_WE, transmission_1_p2
  // NOT_Gate not_3 has open pins: in=li_WE, out=open
  // Transmission_Gate #(.width(2)) transmission_4: pin names not known; wires that end beside it: rs1, add_WE, transmission_4_p3
  // NOT_Gate not_4 has open pins: in=add_WE, out=open
  // Transmission_Gate #(.width(2)) transmission_5: pin names not known; wires that end beside it: rs2, add_WE, transmission_5_p3
  // NOT_Gate not_5 has open pins: in=add_WE, out=open
  // Transmission_Gate #(.width(2)) transmission_6: pin names not known; wires that end beside it: rd, add_WE, transmission_1_p2
  // NOT_Gate not_6 has open pins: in=add_WE, out=open
  // Transmission_Gate #(.width(4)) transmission_7: pin names not known; wires that end beside it: addr_t, bner0_WE, transmission_7_p3, ADDR
  not not_7 (transmission_7_p3, bner0_WE);
  // Transmission_Gate #(.width(2)) transmission_8: pin names not known; wires that end beside it: rs2, bner0_WE, transmission_8_p3, transmission_5_p3
  not not_8 (transmission_8_p3, bner0_WE);
  not not_9 (not_9_out, out_WE);
  Hex_Digit_Display hex_digit_display_1 (.value(pc_4bit_1_output_addr));  // open: dp
  PC_4bit pc_4bit_1 (.ADDR(ADDR), .CP(CP), .EN(WE), .clk(clk), .RST(RST), .output_ADDR(pc_4bit_1_output_addr));
  // Transmission_Gate #(.width(8)) transmission_9: pin names not known; wires that end beside it: Dout, out_WE, not_9_out, outline
  // Transmission_Gate #(.width(8)) transmission_10: pin names not known; wires that end beside it: Dout1, add_WE, transmission_10_p3, transmission_10_p4
  not not_10 (transmission_10_p3, add_WE);
  // Transmission_Gate #(.width(8)) transmission_11: pin names not known; wires that end beside it: Dout2, add_WE, transmission_11_p3
  // NOT_Gate not_11 has open pins: in=add_WE, out=open
  Adder adder_1 (.a(transmission_10_p4), .b(transmission_11_p3), .out(transmission_2_p2));  // open: cin, cout
  // NOT_Gate not_12 has open pins: in=comparator_1_eq, out=open
  Comparator comparator_1 (.a(Dout2), .b(rd0), .eq(comparator_1_eq));  // open: gt, lt
  not not_13 (not_13_out, bner0_WE);
  not not_14 (not_14_out, bner0_WE);
  // Transmission_Gate transmission_12: pin names not known; wires that end beside it: bner0_WE, not_13_out, CP
  // Transmission_Gate transmission_13: pin names not known; wires that end beside it: 1'b0, bner0_WE, not_14_out, CP
  ROM_8 rom_8_1 (.ADDR(pc_4bit_1_output_addr), .instruction(rom_8_1_instruction));
  Hex_Digit_Display hex_digit_display_2 (.value(rom_8_1_instruction[7:4]));  // open: dp
  Hex_Digit_Display hex_digit_display_3 (.value(rom_8_1_instruction[3:0]));  // open: dp
  Multiplexer multiplexer_1 (.in0(WE), .in1(1'b0), .out(multiplexer_1_out), .sel(bner0_WE));
  Hex_Digit_Display hex_digit_display_4 (.value(rd0[7:4]));  // open: dp
  Hex_Digit_Display hex_digit_display_5 (.value(outline[7:4]));  // open: dp
  Hex_Digit_Display hex_digit_display_6 (.value(rd0[3:0]));  // open: dp
  Hex_Digit_Display hex_digit_display_7 (.value(rd1[7:4]));  // open: dp
  Hex_Digit_Display hex_digit_display_8 (.value(outline[3:0]));  // open: dp
  Decoder_instruction decoder_instruction_1 (
    .instruction(rom_8_1_instruction), .opcode(opcode), .rd(rd), .rs1(rs1), .rs2(rs2), .imm(imm),
    .addr(addr_t), .rdout(rdout));
  Hex_Digit_Display hex_digit_display_9 (.value(rd1[3:0]));  // open: dp
  Hex_Digit_Display hex_digit_display_10 (.value(rd2[7:4]));  // open: dp
  GPR_4_8 gpr_4_8_1 (
    .Din(transmission_2_p2), .rd(transmission_1_p2), .rs1(transmission_4_p3), .rs2(transmission_5_p3),
    .WE(multiplexer_1_out), .clk(clk), .RST(RST), .Dout(Dout), .Dout1(Dout1), .Dout2(Dout2), .rd0(rd0),
    .rd1(rd1), .rd2(rd2), .rd3(rd3));
  Hex_Digit_Display hex_digit_display_11 (.value(rd2[3:0]));  // open: dp
  Hex_Digit_Display hex_digit_display_12 (.value(rd3[7:4]));  // open: dp
  Hex_Digit_Display hex_digit_display_13 (.value(rd3[3:0]));  // open: dp
  CU cu_1 (.opcode(opcode), .add_WE(add_WE), .out_WE(out_WE), .li_WE(li_WE), .bner0_WE(bner0_WE));

  // Other names for the same wires on the sheet: imm_8[3:0] = imm
endmodule

module ROM_8 (
  input  [3:0] ADDR,
  output [7:0] instruction
);

  // Probe on 8'h8a
  // Probe on 8'h90
  // Probe on 8'ha0
  // Probe on 8'hb1
  // Probe on 8'h17
  // Probe on 8'h29
  // Probe on 8'hd1
  // Probe on 8'hdf
  // Probe on 8'h8b
  // Probe on 8'h91
  // Probe on 8'ha0
  // Probe on 8'hb2
  // Probe on 8'h29
  // Probe on 8'h17
  // Probe on 8'hd1
  // Probe on 8'hdf
  Multiplexer #(.select(4), .width(8)) multiplexer_1 (
    .in0(8'h8b), .in1(8'h91), .in2(8'ha0), .in3(8'hb2), .in4(8'h29), .in5(8'h17), .in6(8'hd1), .in7(8'h60),
    .in8(8'hdf), .out(instruction), .sel(ADDR));  // open: in9, in10, in11, in12, in13, in14, in15
  // Probe on 8'h8b
  // Probe on 8'h91
  // Probe on 8'ha0
  // Probe on 8'hb2
  // Probe on 8'h29
  // Probe on 8'h17
  // Probe on 8'hd1
  // Probe on 8'h60
  // Probe on 8'hdf
endmodule

module PC_4bit (
  input  [3:0] ADDR,
  input  CP,
  input  EN,
  input  clk,
  input  RST,
  output [3:0] output_ADDR
);

  wire not_1_out, transmission_2_p2;
  wire [3:0] transmission_1_p4;

  Adder #(.width(4)) adder_1 (.a(4'b0001), .b(output_ADDR));  // open: out, cin, cout
  not not_1 (not_1_out, CP);
  // Transmission_Gate #(.width(4)) transmission_1: pin names not known; wires that end beside it: ADDR, not_1_out, CP, transmission_1_p4
  // Transmission_Gate #(.width(4)) transmission_2: pin names not known; wires that end beside it: CP, transmission_2_p2, transmission_1_p4
  Register #(.width(4)) PC (.D(transmission_1_p4), .en(EN), .clk(clk), .Q(output_ADDR), .clr(RST));
  not not_2 (transmission_2_p2, CP);
endmodule

module RAM_8_8 (
  input  [7:0] Din,
  input  [2:0] A,
  input  WE,
  input  clk,
  input  R,
  output [7:0] Dout
);

  wire Sel_0, Sel_1, Sel_2, Sel_3, Sel_4, Sel_5, Sel_6, Sel_7, WE0, WE1, WE2, WE3, WE4, WE5, WE6, WE7;
  wire [7:0] D0, D1, D2, D3, D4, D5, D6, D7, Q0, Q1, Q2, Q3, Q4, Q5, Q6, Q7;

  Demultiplexer #(.select(3), .width(8)) demultiplexer_1 (
    .out0(D0), .out1(D1), .out2(D2), .out3(D3), .out4(D4), .out5(D5), .out6(D6), .out7(D7), .in(Din), .sel(A));
  and and_1 (WE0, WE, Sel_0);
  and and_2 (WE1, WE, Sel_1);
  and and_3 (WE2, WE, Sel_2);
  and and_4 (WE3, WE, Sel_3);
  and and_5 (WE4, WE, Sel_4);
  and and_6 (WE5, WE, Sel_5);
  and and_7 (WE6, WE, Sel_6);
  and and_8 (WE7, WE, Sel_7);
  Decoder #(.select(3)) decoder_1 (
    .out0(Sel_0), .out1(Sel_1), .out2(Sel_2), .out3(Sel_3), .out4(Sel_4), .out5(Sel_5), .out6(Sel_6),
    .out7(Sel_7), .sel(A));  // open: en
  Register register_1 (.D(D0), .en(WE0), .clk(clk), .Q(Q0), .clr(R));
  Register register_2 (.D(D1), .en(WE1), .clk(clk), .Q(Q1), .clr(R));
  Register register_3 (.D(D2), .en(WE2), .clk(clk), .Q(Q2), .clr(R));
  Register register_4 (.D(D3), .en(WE3), .clk(clk), .Q(Q3), .clr(R));
  Register register_5 (.D(D4), .en(WE4), .clk(clk), .Q(Q4), .clr(R));
  Register register_6 (.D(D5), .en(WE5), .clk(clk), .Q(Q5), .clr(R));
  Register register_7 (.D(D6), .en(WE6), .clk(clk), .Q(Q6), .clr(R));
  Register register_8 (.D(D7), .en(WE7), .clk(clk), .Q(Q7), .clr(R));
  Multiplexer #(.select(3), .width(8)) multiplexer_1 (
    .in0(Q0), .in1(Q1), .in2(Q2), .in3(Q3), .in4(Q4), .in5(Q5), .in6(Q6), .in7(Q7), .out(Dout), .sel(A));
endmodule

module CU (
  input  [1:0] opcode,
  output add_WE,
  output out_WE,
  output li_WE,
  output bner0_WE
);

  Comparator #(.width(2)) comparator_1 (.a(opcode), .b(2'b00), .eq(add_WE));  // open: gt, lt
  Comparator #(.width(2)) comparator_2 (.a(opcode), .b(2'b01), .eq(out_WE));  // open: gt, lt
  Comparator #(.width(2)) comparator_3 (.a(opcode), .b(2'b10), .eq(li_WE));  // open: gt, lt
  Comparator #(.width(2)) comparator_4 (.a(opcode), .b(2'b11), .eq(bner0_WE));  // open: gt, lt
endmodule

module GPR_4_8 (
  input  [7:0] Din,
  input  [1:0] rd,
  input  [1:0] rs1,
  input  [1:0] rs2,
  input  WE,
  input  clk,
  input  RST,
  output [7:0] Dout,
  output [7:0] Dout1,
  output [7:0] Dout2,
  output [7:0] rd0,
  output [7:0] rd1,
  output [7:0] rd2,
  output [7:0] rd3
);

  wire Sel_0, Sel_1, Sel_2, Sel_3, WE0, WE1, WE2, WE3;

  Decoder #(.select(2)) decoder_1 (.out0(Sel_0), .out1(Sel_1), .out2(Sel_2), .out3(Sel_3), .sel(rd));  // open: en
  and and_1 (WE0, WE, Sel_0);
  and and_2 (WE1, WE, Sel_1);
  and and_3 (WE2, WE, Sel_2);
  and and_4 (WE3, WE, Sel_3);
  Multiplexer #(.select(2), .width(8)) multiplexer_1 (.in0(rd0), .in1(rd1), .in2(rd2), .in3(rd3), .out(Dout), .sel(rd));
  Multiplexer #(.select(2), .width(8)) multiplexer_2 (
    .in0(rd0), .in1(rd1), .in2(rd2), .in3(rd3), .out(Dout1), .sel(rs1));
  Multiplexer #(.select(2), .width(8)) multiplexer_3 (
    .in0(rd0), .in1(rd1), .in2(rd2), .in3(rd3), .out(Dout2), .sel(rs2));
  Register register_1 (.D(Din), .en(WE0), .clk(clk), .Q(rd0), .clr(RST));
  Register register_2 (.D(Din), .en(WE1), .clk(clk), .Q(rd1), .clr(RST));
  Register register_3 (.D(Din), .en(WE2), .clk(clk), .Q(rd2), .clr(RST));
  Register register_4 (.D(Din), .en(WE3), .clk(clk), .Q(rd3), .clr(RST));

  // Other names for the same wires on the sheet: ADDR[1:0] = rd; ADDR1[1:0] = rs1; ADDR2[1:0] = rs2; Q0[7:0] = rd0;
  //   Q1[7:0] = rd1; Q2[7:0] = rd2; Q3[7:0] = rd3; R = RST
endmodule

module Decoder_instruction (
  input  [7:0] instruction,
  output [1:0] opcode,
  output [1:0] rd,
  output [1:0] rs1,
  output [1:0] rs2,
  output [3:0] imm,
  output [3:0] addr,
  output [1:0] rdout
);


  assign addr = instruction[5:2];
  assign imm = instruction[3:0];
  assign opcode = instruction[7:6];
  assign rd = instruction[5:4];
  assign rdout = instruction[5:4];
  assign rs1 = instruction[3:2];
  assign rs2 = instruction[1:0];

  // Other names for the same wires on the sheet: i2 = instruction[2]; i3 = instruction[3]; i0 = instruction[0];
  //   i1 = instruction[1]; i6 = instruction[6]; i7 = instruction[7]; i4 = instruction[4]; i5 = instruction[5]
endmodule
