// Logisim project select_q.circ as structural Verilog: 3 circuits, main circuit select_tips
module select_tips (
  input  in_1,
  input  in_2,
  input  S,
  input  [2:0] in_4,
  input  D1,
  input  [2:0] in_6,
  input  [2:0] in_7,
  input  D0,
  input  [2:0] in_9,
  output [2:0] out_10,
  output Y
);

  one_two_one one_two_one_1 (.D1(D1), .S(S), .D0(D0), .Y(Y));
  three_four_one three_four_one_1 (.S1(in_1), .S0(in_2), .D0(in_4), .D1(in_6), .D2(in_7), .D3(in_9), .Y(out_10));

  // Notes on the sheet:
  //   一位2选1选择器
  //   三位4选1选择器
endmodule

module one_two_one (
  input  D1,
  input  S,
  input  D0,
  output Y
);

  wire and_1_out, and_2_out, not_1_out;

  not not_1 (not_1_out, S);
  and and_1 (and_1_out, D1, S);
  and and_2 (and_2_out, not_1_out, D0);
  or or_1 (Y, and_1_out, and_2_out);
endmodule

module three_four_one (
  input  S1,
  input  S0,
  input  [2:0] D0,
  input  [2:0] D1,
  input  [2:0] D2,
  input  [2:0] D3,
  output [2:0] Y
);

  wire and_1_out, and_2_out, and_3_out, and_4_out, not_1_out, not_2_out, not_3_out, not_4_out;

  not not_1 (not_1_out, S1);
  not not_2 (not_2_out, S0);
  not not_3 (not_3_out, not_1_out);
  not not_4 (not_4_out, not_2_out);
  and and_1 (and_1_out, not_1_out, not_2_out);
  and and_2 (and_2_out, not_1_out, not_4_out);
  and and_3 (and_3_out, not_3_out, not_2_out);
  and and_4 (and_4_out, not_3_out, not_4_out);
  // NOT_Gate not_5 has open pins: in=and_1_out, out=open
  // Transmission_Gate #(.width(3)) transmission_1: pin names not known; wires that end beside it: D0, and_1_out, Y
  // NOT_Gate not_6 has open pins: in=and_2_out, out=open
  // Transmission_Gate #(.width(3)) transmission_2: pin names not known; wires that end beside it: D1, and_2_out, Y
  // NOT_Gate not_7 has open pins: in=and_3_out, out=open
  // Transmission_Gate #(.width(3)) transmission_3: pin names not known; wires that end beside it: D2, and_3_out, Y
  // NOT_Gate not_8 has open pins: in=and_4_out, out=open
  // Transmission_Gate #(.width(3)) transmission_4: pin names not known; wires that end beside it: D3, and_4_out, Y
endmodule
