// Logisim project Decoder_2_4to3_8.circ as structural Verilog: 2 circuits, main circuit main
module main (
  input  A00,
  input  A01,
  input  A2,
  input  A1,
  input  A0,
  output Y0,
  output Y1,
  output Y2,
  output Y3,
  output out_10,
  output out_11,
  output out_12,
  output out_13,
  output out_14,
  output out_15,
  output out_16,
  output out_17
);

  wire not_1_out, not_2_out, not_3_out;

  not not_1 (not_1_out, A00);
  not not_2 (not_2_out, A01);
  not not_3 (not_3_out, A2);
  and and_1 (Y0, not_2_out, not_1_out);
  and and_2 (Y1, not_1_out, A00);
  and and_3 (Y2, not_2_out, A01);
  and and_4 (Y3, A00, A01);
  Decoder_2_4 D1 (.S(A2), .A0(A0), .A1(A1), .Y0(out_10), .Y1(out_11), .Y2(out_12), .Y3(out_13));
  Decoder_2_4 D2 (.S(not_3_out), .A0(A0), .A1(A1), .Y0(out_14), .Y1(out_15), .Y2(out_16), .Y3(out_17));

  // Notes on the sheet:
  //   2-4译码器
  //   2个24译码器搭建1个38译码器
endmodule

module Decoder_2_4 (
  input  S,
  input  A0,
  input  A1,
  output Y0,
  output Y1,
  output Y2,
  output Y3
);

  wire not_1_out, not_2_out, not_3_out;

  not not_1 (not_1_out, S);
  not not_2 (not_2_out, A1);
  not not_3 (not_3_out, A0);
  and and_1 (Y0, not_3_out, not_1_out, not_2_out);
  and and_2 (Y1, not_2_out, not_1_out, A0);
  and and_3 (Y2, not_3_out, not_1_out, A1);
  and and_4 (Y3, A0, not_1_out, A1);

  // Notes on the sheet:
  //   2-4译码器
endmodule
