// Logisim project seven_light.circ as structural Verilog: 7 circuits, main circuit tips_seven_light
module tips_seven_light (
  input  in_1,
  input  in_2,
  input  in_3,
  input  in_4,
  input  in_5,
  input  in_6,
  input  in_7,
  input  in_8,
  input  in_9,
  input  in_10,
  input  in_11,
  input  in_12,
  input  in_13,
  input  in_14,
  input  in_15,
  input  in_16,
  input  in_17,
  input  in_18,
  input  in_19,
  input  in_20,
  input  in_21,
  input  in_22,
  input  in_23,
  input  in_24,
  input  in_25,
  input  in_26,
  input  in_27,
  input  in_28,
  input  in_29,
  input  in_30,
  input  in_31,
  input  in_32,
  input  in_33,
  input  in_34,
  input  in_35,
  input  in_36,
  input  in_37,
  input  in_38,
  input  in_39,
  input  in_40,
  input  in_41,
  input  in_42,
  input  in_43,
  input  in_44,
  input  in_45,
  input  A3,
  input  A2,
  input  A1,
  input  A0
);

  wire a_out, b_out, c_out, d_out, e_out, f_out, four_eight_decoder_10_to_light_1_ya,
       four_eight_decoder_10_to_light_1_yb, four_eight_decoder_10_to_light_1_yc,
       four_eight_decoder_10_to_light_1_yd, four_eight_decoder_10_to_light_1_ye,
       four_eight_decoder_10_to_light_1_yf, four_eight_decoder_10_to_light_1_yg,
       four_eight_decoder_10_to_light_1_yh, four_eight_decoder_10_to_light_2_ya,
       four_eight_decoder_10_to_light_2_yb, four_eight_decoder_10_to_light_2_yc,
       four_eight_decoder_10_to_light_2_yd, four_eight_decoder_10_to_light_2_ye,
       four_eight_decoder_10_to_light_2_yf, four_eight_decoder_10_to_light_2_yg,
       four_eight_decoder_10_to_light_2_yh, four_eight_decoder_16_to_light_1_ya,
       four_eight_decoder_16_to_light_1_yb, four_eight_decoder_16_to_light_1_yc,
       four_eight_decoder_16_to_light_1_yd, four_eight_decoder_16_to_light_1_ye,
       four_eight_decoder_16_to_light_1_yf, four_eight_decoder_16_to_light_1_yg,
       four_eight_decoder_16_to_light_2_ya, four_eight_decoder_16_to_light_2_yb,
       four_eight_decoder_16_to_light_2_yc, four_eight_decoder_16_to_light_2_yd,
       four_eight_decoder_16_to_light_2_ye, four_eight_decoder_16_to_light_2_yf,
       four_eight_decoder_16_to_light_2_yg, four_eight_decoder_16_to_light_3_ya,
       four_eight_decoder_16_to_light_3_yb, four_eight_decoder_16_to_light_3_yc,
       four_eight_decoder_16_to_light_3_yd, four_eight_decoder_16_to_light_3_ye,
       four_eight_decoder_16_to_light_3_yf, four_eight_decoder_16_to_light_3_yg,
       four_eight_decoder_16_to_light_4_ya, four_eight_decoder_16_to_light_4_yb,
       four_eight_decoder_16_to_light_4_yc, four_eight_decoder_16_to_light_4_yd,
       four_eight_decoder_16_to_light_4_ye, four_eight_decoder_16_to_light_4_yf,
       four_eight_decoder_16_to_light_4_yg, g_out, not_1_out, sixteen_four_encoder_1_d0,
       sixteen_four_encoder_1_d1, sixteen_four_encoder_1_d2, sixteen_four_encoder_1_d3,
       sixteen_four_priority_four_4_2_1_z0, sixteen_four_priority_four_4_2_1_z1,
       sixteen_four_priority_four_4_2_1_z2, sixteen_four_priority_four_4_2_1_z3;

  not not_1 (not_1_out, in_9);
  four_eight_decoder_10_to_light four_eight_decoder_10_to_light_1 (
    .A3(in_1), .A2(in_3), .A1(in_5), .A0(in_7), .S(not_1_out), .Ya(four_eight_decoder_10_to_light_1_ya),
    .Yg(four_eight_decoder_10_to_light_1_yg), .Yd(four_eight_decoder_10_to_light_1_yd),
    .Yh(four_eight_decoder_10_to_light_1_yh), .Yb(four_eight_decoder_10_to_light_1_yb),
    .Ye(four_eight_decoder_10_to_light_1_ye), .Yf(four_eight_decoder_10_to_light_1_yf),
    .Yc(four_eight_decoder_10_to_light_1_yc));
  four_eight_decoder_16_to_light four_eight_decoder_16_to_light_1 (
    .A3(in_21), .A2(in_23), .A1(in_25), .A0(in_26), .S(in_27), .Ye(four_eight_decoder_16_to_light_1_ye),
    .Yc(four_eight_decoder_16_to_light_1_yc), .Ya(four_eight_decoder_16_to_light_1_ya),
    .Yg(four_eight_decoder_16_to_light_1_yg), .Yf(four_eight_decoder_16_to_light_1_yf),
    .Yd(four_eight_decoder_16_to_light_1_yd), .Yb(four_eight_decoder_16_to_light_1_yb));
  _7_Segment_Display u_7_segment_display_1 (
    .g(four_eight_decoder_10_to_light_1_yg), .f(four_eight_decoder_10_to_light_1_yf),
    .a(four_eight_decoder_10_to_light_1_ya), .b(four_eight_decoder_10_to_light_1_yb),
    .e(four_eight_decoder_10_to_light_1_ye), .d(four_eight_decoder_10_to_light_1_yd),
    .c(four_eight_decoder_10_to_light_1_yc), .dp(four_eight_decoder_10_to_light_1_yh));
  _7_Segment_Display u_7_segment_display_2 (
    .g(four_eight_decoder_16_to_light_1_yg), .f(four_eight_decoder_16_to_light_1_yf),
    .a(four_eight_decoder_16_to_light_1_ya), .b(four_eight_decoder_16_to_light_1_yb),
    .e(four_eight_decoder_16_to_light_1_ye), .d(four_eight_decoder_16_to_light_1_yd),
    .c(four_eight_decoder_16_to_light_1_yc), .dp(1'b0));
  four_eight_decoder_10_to_light four_eight_decoder_10_to_light_2 (
    .A3(A3), .A2(A2), .A1(A1), .A0(A0), .S(in_45), .Ya(four_eight_decoder_10_to_light_2_ya),
    .Yg(four_eight_decoder_10_to_light_2_yg), .Yd(four_eight_decoder_10_to_light_2_yd),
    .Yh(four_eight_decoder_10_to_light_2_yh), .Yb(four_eight_decoder_10_to_light_2_yb),
    .Ye(four_eight_decoder_10_to_light_2_ye), .Yf(four_eight_decoder_10_to_light_2_yf),
    .Yc(four_eight_decoder_10_to_light_2_yc));
  four_eight_decoder_16_to_light four_eight_decoder_16_to_light_2 (
    .A3(A3), .A2(A2), .A1(A1), .A0(A0), .S(in_45), .Ye(four_eight_decoder_16_to_light_2_ye),
    .Yc(four_eight_decoder_16_to_light_2_yc), .Ya(four_eight_decoder_16_to_light_2_ya),
    .Yg(four_eight_decoder_16_to_light_2_yg), .Yf(four_eight_decoder_16_to_light_2_yf),
    .Yd(four_eight_decoder_16_to_light_2_yd), .Yb(four_eight_decoder_16_to_light_2_yb));
  or a (a_out, four_eight_decoder_16_to_light_2_ya, four_eight_decoder_10_to_light_2_ya);
  or d (d_out, four_eight_decoder_10_to_light_2_yd, four_eight_decoder_16_to_light_2_yd);
  or b (b_out, four_eight_decoder_10_to_light_2_yb, four_eight_decoder_16_to_light_2_yb);
  or c (c_out, four_eight_decoder_10_to_light_2_yc, four_eight_decoder_16_to_light_2_yc);
  or e (e_out, four_eight_decoder_16_to_light_2_ye, four_eight_decoder_10_to_light_2_ye);
  or g (g_out, four_eight_decoder_10_to_light_2_yg, four_eight_decoder_16_to_light_2_yg);
  or f (f_out, four_eight_decoder_16_to_light_2_yf, four_eight_decoder_10_to_light_2_yf);
  _7_Segment_Display u_7_segment_display_3 (
    .g(g_out), .f(f_out), .a(a_out), .b(b_out), .e(e_out), .d(d_out), .c(c_out),
    .dp(four_eight_decoder_10_to_light_2_yh));
  sixteen_four_encoder sixteen_four_encoder_1 (
    .I15(in_2), .I14(in_4), .I13(in_6), .I12(in_8), .I11(in_10), .I10(in_12), .I9(in_13), .I8(in_14),
    .I7(in_15), .I6(in_16), .I5(in_17), .I4(in_18), .I3(in_19), .I2(in_20), .I1(in_22), .I0(in_24),
    .D3(sixteen_four_encoder_1_d3), .D2(sixteen_four_encoder_1_d2), .D1(sixteen_four_encoder_1_d1),
    .D0(sixteen_four_encoder_1_d0));
  sixteen_four_priority_four_4_2 sixteen_four_priority_four_4_2_1 (
    .A0(in_28), .A1(in_29), .A2(in_30), .A3(in_31), .A4(in_32), .A5(in_34), .A6(in_35), .A7(in_36),
    .A8(in_37), .A9(in_38), .A10(in_39), .A11(in_40), .A12(in_41), .A13(in_42), .A14(in_43), .A15(in_44),
    .Z3(sixteen_four_priority_four_4_2_1_z3), .Z2(sixteen_four_priority_four_4_2_1_z2),
    .Z1(sixteen_four_priority_four_4_2_1_z1), .Z0(sixteen_four_priority_four_4_2_1_z0));
  four_eight_decoder_16_to_light four_eight_decoder_16_to_light_3 (
    .A3(sixteen_four_encoder_1_d3), .A2(sixteen_four_encoder_1_d2), .A1(sixteen_four_encoder_1_d1),
    .A0(sixteen_four_encoder_1_d0), .S(in_11), .Ye(four_eight_decoder_16_to_light_3_ye),
    .Yc(four_eight_decoder_16_to_light_3_yc), .Ya(four_eight_decoder_16_to_light_3_ya),
    .Yg(four_eight_decoder_16_to_light_3_yg), .Yf(four_eight_decoder_16_to_light_3_yf),
    .Yd(four_eight_decoder_16_to_light_3_yd), .Yb(four_eight_decoder_16_to_light_3_yb));
  _7_Segment_Display u_7_segment_display_4 (
    .g(four_eight_decoder_16_to_light_3_yg), .f(four_eight_decoder_16_to_light_3_yf),
    .a(four_eight_decoder_16_to_light_3_ya), .b(four_eight_decoder_16_to_light_3_yb),
    .e(four_eight_decoder_16_to_light_3_ye), .d(four_eight_decoder_16_to_light_3_yd),
    .c(four_eight_decoder_16_to_light_3_yc), .dp(1'b0));
  four_eight_decoder_16_to_light four_eight_decoder_16_to_light_4 (
    .A3(sixteen_four_priority_four_4_2_1_z3), .A2(sixteen_four_priority_four_4_2_1_z2),
    .A1(sixteen_four_priority_four_4_2_1_z1), .A0(sixteen_four_priority_four_4_2_1_z0), .S(in_33),
    .Ye(four_eight_decoder_16_to_light_4_ye), .Yc(four_eight_decoder_16_to_light_4_yc),
    .Ya(four_eight_decoder_16_to_light_4_ya), .Yg(four_eight_decoder_16_to_light_4_yg),
    .Yf(four_eight_decoder_16_to_light_4_yf), .Yd(four_eight_decoder_16_to_light_4_yd),
    .Yb(four_eight_decoder_16_to_light_4_yb));
  _7_Segment_Display u_7_segment_display_5 (
    .g(four_eight_decoder_16_to_light_4_yg), .f(four_eight_decoder_16_to_light_4_yf),
    .a(four_eight_decoder_16_to_light_4_ya), .b(four_eight_decoder_16_to_light_4_yb),
    .e(four_eight_decoder_16_to_light_4_ye), .d(four_eight_decoder_16_to_light_4_yd),
    .c(four_eight_decoder_16_to_light_4_yc), .dp(1'b0));

  // Notes on the sheet:
  //   十六进制
  //   十进制
  //   选择器切换10进制与16进制
  //   七段数码管相关案例
  //   16-4
  //   16-4（4-2）优先
endmodule

module four_eight_decoder_10_to_light (
  input  A3,
  input  A2,
  input  A1,
  input  A0,
  input  S,
  output Ya,
  output Yg,
  output Yd,
  output Yh,
  output Yb,
  output Ye,
  output Yf,
  output Yc
);

  wire and_1_out, and_2_out, and_3_out, and_4_out, and_5_out, and_6_out, and_7_out, and_8_out, and_9_out,
       and_10_out, and_11_out, and_15_out, and_16_out, and_17_out, and_18_out, and_19_out, and_20_out,
       and_21_out, and_22_out, and_23_out, and_24_out, and_25_out, and_29_out, and_30_out, and_31_out,
       and_32_out, and_33_out, and_34_out, or_1_out, or_2_out, or_3_out, or_4_out, or_5_out, or_6_out,
       or_7_out, or_8_out, S_t;

  not not_1 (S_t, S);
  and and_1 (and_1_out, ~A3, A1);  // AND_Gate
  and and_2 (and_2_out, ~A3, A2, A0);  // AND_Gate
  and and_3 (and_3_out, A3, ~A2, ~A1);  // AND_Gate
  and and_4 (and_4_out, ~A2, ~A1, ~A0);  // AND_Gate
  and and_5 (and_5_out, ~A2, ~A1);  // AND_Gate
  and and_6 (and_6_out, ~A3, ~A2);  // AND_Gate
  and and_7 (and_7_out, ~A3, A1, A0);  // AND_Gate
  and and_8 (and_8_out, ~A3, ~A1, ~A0);  // AND_Gate
  and and_9 (and_9_out, ~A3, A0);  // AND_Gate
  and and_10 (and_10_out, ~A3, A2);  // AND_Gate
  and and_11 (and_11_out, ~A2, ~A1);  // AND_Gate
  or or_1 (or_1_out, and_1_out, and_2_out, and_3_out, and_4_out);
  and and_12 (Ya, or_1_out, S_t);
  or or_2 (or_2_out, and_5_out, and_6_out, and_7_out, and_8_out);
  and and_13 (Yb, or_2_out, S_t);
  or or_3 (or_3_out, and_9_out, and_10_out, and_11_out);
  and and_14 (Yc, or_3_out, S_t);
  and and_15 (and_15_out, ~A3, A1, ~A0);  // AND_Gate
  and and_16 (and_16_out, ~A3, ~A2, A1);  // AND_Gate
  and and_17 (and_17_out, A3, ~A2, ~A1);  // AND_Gate
  and and_18 (and_18_out, ~A2, ~A1, ~A0);  // AND_Gate
  and and_19 (and_19_out, ~A3, A2, ~A1, A0);  // AND_Gate
  and and_20 (and_20_out, ~A3, A1, ~A0);  // AND_Gate
  and and_21 (and_21_out, ~A2, ~A1, ~A0);  // AND_Gate
  and and_22 (and_22_out, ~A3, A2, ~A0);  // AND_Gate
  and and_23 (and_23_out, ~A3, A2, ~A1);  // AND_Gate
  and and_24 (and_24_out, A3, ~A2, ~A1);  // AND_Gate
  and and_25 (and_25_out, ~A2, ~A1, ~A0);  // AND_Gate
  or or_4 (or_4_out, and_15_out, and_16_out, and_17_out, and_18_out, and_19_out);
  and and_26 (Yd, or_4_out, S_t);
  or or_5 (or_5_out, and_20_out, and_21_out);
  and and_27 (Ye, or_5_out, S_t);
  or or_6 (or_6_out, and_22_out, and_23_out, and_24_out, and_25_out);
  and and_28 (Yf, or_6_out, S_t);
  and and_29 (and_29_out, ~A3, ~A2, A1);  // AND_Gate
  and and_30 (and_30_out, ~A3, A2, ~A0);  // AND_Gate
  and and_31 (and_31_out, ~A3, A2, ~A1);  // AND_Gate
  and and_32 (and_32_out, A3, ~A2, ~A1);  // AND_Gate
  and and_33 (and_33_out, A3, A1);
  and and_34 (and_34_out, A3, A2);
  or or_7 (or_7_out, and_29_out, and_30_out, and_31_out, and_32_out);
  and and_35 (Yg, or_7_out, S_t);
  or or_8 (or_8_out, and_33_out, and_34_out);
  and and_36 (Yh, or_8_out, S_t);

  // Notes on the sheet:
  //   四输入八输出
endmodule

module four_eight_decoder_16_to_light (
  input  A3,
  input  A2,
  input  A1,
  input  A0,
  input  S,
  output Ye,
  output Yc,
  output Ya,
  output Yg,
  output Yf,
  output Yd,
  output Yb
);

  wire and_1_out, and_2_out, and_3_out, and_4_out, and_5_out, and_6_out, and_7_out, and_8_out, and_9_out,
       and_10_out, and_11_out, and_14_out, and_15_out, and_16_out, and_17_out, and_18_out, and_19_out,
       and_20_out, and_21_out, and_22_out, and_23_out, and_26_out, and_27_out, and_28_out, and_29_out,
       and_30_out, and_31_out, and_32_out, and_33_out, and_34_out, and_37_out, and_38_out, and_39_out,
       and_40_out, and_41_out, or_1_out, or_2_out, or_3_out, or_4_out, or_5_out, or_6_out, or_7_out;

  and and_1 (and_1_out, A2, A1);
  and and_2 (and_2_out, ~A3, A1);  // AND_Gate
  and and_3 (and_3_out, A3, ~A0);  // AND_Gate
  and and_4 (and_4_out, ~A2, ~A0);  // AND_Gate
  and and_5 (and_5_out, ~A3, A2, A0);  // AND_Gate
  and and_6 (and_6_out, A3, ~A2, ~A1);  // AND_Gate
  and and_7 (and_7_out, ~A2, ~A0);  // AND_Gate
  and and_8 (and_8_out, ~A2, ~A1);  // AND_Gate
  and and_9 (and_9_out, ~A3, A1, A0);  // AND_Gate
  and and_10 (and_10_out, A3, ~A1, A0);  // AND_Gate
  and and_11 (and_11_out, ~A3, ~A1, ~A0);  // AND_Gate
  or or_1 (or_1_out, and_1_out, and_2_out, and_3_out, and_4_out, and_5_out, and_6_out);
  and and_12 (Ya, or_1_out, S);
  or or_2 (or_2_out, and_7_out, and_8_out, and_9_out, and_10_out, and_11_out);
  and and_13 (Yb, or_2_out, S);
  and and_14 (and_14_out, ~A1, A0);  // AND_Gate
  and and_15 (and_15_out, ~A2, A0);  // AND_Gate
  and and_16 (and_16_out, ~A3, A2);  // AND_Gate
  and and_17 (and_17_out, A3, ~A2);  // AND_Gate
  and and_18 (and_18_out, ~A2, ~A1);  // AND_Gate
  and and_19 (and_19_out, A3, ~A1);  // AND_Gate
  and and_20 (and_20_out, ~A2, A1, A0);  // AND_Gate
  and and_21 (and_21_out, A2, ~A1, A0);  // AND_Gate
  and and_22 (and_22_out, A2, A1, ~A0);  // AND_Gate
  and and_23 (and_23_out, ~A3, ~A2, ~A0);  // AND_Gate
  or or_3 (or_3_out, and_14_out, and_15_out, and_16_out, and_17_out, and_18_out);
  or or_4 (or_4_out, and_19_out, and_20_out, and_21_out, and_22_out, and_23_out);
  and and_24 (Yc, or_3_out, S);
  and and_25 (Yd, or_4_out, S);
  and and_26 (and_26_out, A3, A1);
  and and_27 (and_27_out, A3, A2);
  and and_28 (and_28_out, A1, ~A0);  // AND_Gate
  and and_29 (and_29_out, ~A2, ~A0);  // AND_Gate
  and and_30 (and_30_out, A3, A1);
  and and_31 (and_31_out, A2, ~A0);  // AND_Gate
  and and_32 (and_32_out, A3, ~A2);  // AND_Gate
  and and_33 (and_33_out, ~A1, ~A0);  // AND_Gate
  and and_34 (and_34_out, ~A3, A2, ~A1);  // AND_Gate
  or or_5 (or_5_out, and_26_out, and_27_out, and_28_out, and_29_out);
  and and_35 (Ye, or_5_out, S);
  or or_6 (or_6_out, and_30_out, and_31_out, and_32_out, and_33_out, and_34_out);
  and and_36 (Yf, or_6_out, S);
  and and_37 (and_37_out, A3, A0);
  and and_38 (and_38_out, A1, ~A0);  // AND_Gate
  and and_39 (and_39_out, ~A2, A1);  // AND_Gate
  and and_40 (and_40_out, A3, ~A2);  // AND_Gate
  and and_41 (and_41_out, ~A3, A2, ~A1);  // AND_Gate
  or or_7 (or_7_out, and_37_out, and_38_out, and_39_out, and_40_out, and_41_out);
  and and_42 (Yg, or_7_out, S);

  // Notes on the sheet:
  //   四输出八输出16进制
endmodule

module sixteen_four_encoder (
  input  I15,
  input  I14,
  input  I13,
  input  I12,
  input  I11,
  input  I10,
  input  I9,
  input  I8,
  input  I7,
  input  I6,
  input  I5,
  input  I4,
  input  I3,
  input  I2,
  input  I1,
  input  I0,
  output D3,
  output D2,
  output D1,
  output D0
);

  or or_1 (D3, I15, I14, I13, I12, I11, I10, I9, I8);
  or or_2 (D2, I15, I14, I13, I12, I7, I6, I5, I4);
  or or_3 (D1, I15, I14, I11, I10, I7, I6, I3, I2);
  or or_4 (D0, I15, I13, I11, I9, I7, I5, I3, I1);
endmodule

module four_two_priority (
  input  A3,
  input  A2,
  input  S,
  input  A1,
  input  A0,
  output Y1,
  output Y0,
  output YS_bar,
  output YEX_bar
);

  wire and_1_out, not_1_out, not_2_out, not_3_out, not_4_out, not_5_out, or_1_out, or_2_out;

  and and_1 (and_1_out, ~A2, A1);  // AND_Gate
  not not_1 (not_1_out, A3);
  not not_2 (not_2_out, A2);
  not not_3 (not_3_out, A1);
  not not_4 (not_4_out, A0);
  or or_1 (or_1_out, A3, A2);
  or or_2 (or_2_out, A3, and_1_out);
  not not_5 (not_5_out, S);
  and and_2 (Y1, or_1_out, not_5_out);
  and and_3 (Y0, not_5_out, or_2_out);
  nand nand_1 (YS_bar, not_1_out, not_2_out, not_3_out, not_4_out, not_5_out);
  nand nand_2 (YEX_bar, YS_bar, not_5_out);

  // Notes on the sheet:
  //   4-2优先编码器（加控制器）
endmodule

module four_two_encoder (
  input  A3,
  input  A2,
  input  A1,
  input  A0,
  output Y1,
  output Y0
);

  wire and_1_out, and_2_out, and_3_out;

  and and_1 (and_1_out, ~A3, A2, ~A1, ~A0);  // AND_Gate
  and and_2 (and_2_out, A3, ~A2, ~A1, ~A0);  // AND_Gate
  and and_3 (and_3_out, ~A3, ~A2, A1, ~A0);  // AND_Gate
  or or_1 (Y1, and_1_out, and_2_out);
  or or_2 (Y0, and_2_out, and_3_out);

  // Notes on the sheet:
  //   4-2编码器
endmodule

module sixteen_four_priority_four_4_2 (
  input  A0,
  input  A1,
  input  A2,
  input  A3,
  input  A4,
  input  A5,
  input  A6,
  input  A7,
  input  A8,
  input  A9,
  input  A10,
  input  A11,
  input  A12,
  input  A13,
  input  A14,
  input  A15,
  output Z3,
  output Z2,
  output Z1,
  output Z0
);

  wire four_two_priority_1_y0, four_two_priority_1_y1, four_two_priority_2_y0, four_two_priority_2_y1,
       four_two_priority_2_yex_bar, four_two_priority_2_ys_bar, four_two_priority_3_y0,
       four_two_priority_3_y1, four_two_priority_4_y0, four_two_priority_4_y1, four_two_priority_4_yex_bar,
       four_two_priority_4_ys_bar, nand_1_out, nand_2_out, nand_3_out, nand_4_out, not_1_out, not_2_out;

  nand nand_1 (nand_1_out, ~four_two_priority_1_y0, ~four_two_priority_2_y0);  // NAND_Gate
  four_two_priority four_two_priority_1 (
    .A3(A3), .A2(A2), .S(four_two_priority_2_ys_bar), .A1(A1), .A0(A0), .Y1(four_two_priority_1_y1),
    .Y0(four_two_priority_1_y0));  // open: YS_bar, YEX_bar
  nand nand_2 (nand_2_out, ~four_two_priority_1_y1, ~four_two_priority_2_y1);  // NAND_Gate
  four_two_priority four_two_priority_2 (
    .A3(A7), .A2(A6), .S(Z3), .A1(A5), .A0(A4), .Y1(four_two_priority_2_y1), .Y0(four_two_priority_2_y0),
    .YS_bar(four_two_priority_2_ys_bar), .YEX_bar(four_two_priority_2_yex_bar));
  not not_1 (not_1_out, four_two_priority_2_yex_bar);
  four_two_priority four_two_priority_3 (
    .A3(A11), .A2(A10), .S(four_two_priority_4_ys_bar), .A1(A9), .A0(A8), .Y1(four_two_priority_3_y1),
    .Y0(four_two_priority_3_y0), .YS_bar(Z3));  // open: YEX_bar
  nand nand_3 (nand_3_out, ~four_two_priority_3_y0, ~four_two_priority_4_y0);  // NAND_Gate
  nand nand_4 (nand_4_out, ~four_two_priority_3_y1, ~four_two_priority_4_y1);  // NAND_Gate
  or or_1 (Z2, not_1_out, not_2_out);
  or or_2 (Z1, nand_2_out, nand_4_out);
  not not_2 (not_2_out, four_two_priority_4_yex_bar);
  or or_3 (Z0, nand_1_out, nand_3_out);
  four_two_priority four_two_priority_4 (
    .A3(A15), .A2(A14), .S(1'b0), .A1(A13), .A0(A12), .Y1(four_two_priority_4_y1),
    .Y0(four_two_priority_4_y0), .YS_bar(four_two_priority_4_ys_bar), .YEX_bar(four_two_priority_4_yex_bar));

  // Notes on the sheet:
  //   16-4优先译码器
endmodule
